# Fritzing sketch 555AstableAndMono (saved by Fritzing 0.9.10b)
breadboards: 1

parts:
  U1 = 555 Timer [package="DIP8 [THT]"]
  R2 = Resistor [tolerance=±5% power=0.25 resistance=10k package=THT]
  C2 = Electrolytic Capacitor [capacitance=1µF voltage=16V package="0807 [SMD, electrolytic]"]
  R1 = Resistor [tolerance=±20% power=0.25 resistance=1000 package=THT]
  C1 = Ceramic Capacitor [capacitance=100nF voltage=35V package="100 mil [THT, multilayer]"]
  R3 = Resistor [tolerance=±5% power=0.25 resistance=220 package=THT]
  LED1 = LED - 5mm [color="White (4500K)" current=0.030 package="5 mm [THT]"]
  U2 = 555 Timer [package="DIP8 [THT]"]
  S2 = Pushbutton [package="[THT]"]
  C3 = Ceramic Capacitor [capacitance=100nF voltage=35V package="100 mil [THT, multilayer]"]
  R6 = Resistor [tolerance=±5% power=0.25 resistance=1000 package=THT]
  R7 = Resistor [tolerance=±5% power=0.25 resistance=1M package=THT]
  C4 = Electrolytic Capacitor [capacitance=1µF voltage=16V package="0807 [SMD, electrolytic]"]
  R8 = TRIMPOT [maximum_resistance=10kΩ knob_status=50% power=0.5W package=trimpot_pth_s3_lock]

nets:
  N1: U1.Ground, C2.-, C1.0, LED1.cathode, U2.Ground, S2.Pin_1, S2.Pin_2, C3.0, C4.-
  N2: U1.Trigger, U1.Threshold, C2.+, R8.CCW
  N3: U1.Output, R3.Pin_0
  N4: U1.Reset, U1.Vcc_Supply_Voltage, R1.Pin_1, U2.Reset, U2.Vcc_Supply_Voltage, R6.Pin_1, R7.Pin_0
  N5: U1.Control_Voltage, C1.1
  N6: U1.Discharge, R2.Pin_0, R1.Pin_0
  N7: R2.Pin_1, R8.WIPER
  N8: R3.Pin_1, LED1.anode
  N9: U2.Trigger, S2.Pin_3, S2.Pin_4, R7.Pin_1
  N10: U2.Control_Voltage, C3.1
  N11: U2.Threshold, U2.Discharge, R6.Pin_0, C4.+
