# Fritzing sketch 556DualModeTimer (saved by Fritzing 0.9.10b)
breadboards: 1

parts:
  U1 = 556 [package=dil14]
  R1 = Resistor [tolerance=±5% power=0.5W resistance=1k package=THT]
  R2 = Resistor [tolerance=±5% power=0.25 resistance=1k package=THT]
  C1 = Electrolytic Capacitor [capacitance=1µF voltage=35V package="100 mil [THT, electrolytic]"]
  R4 = TRIMPOT [maximum_resistance=10kΩ knob_status=50% power=0.5W package=trimpot_pth_s3_lock]
  C2 = Ceramic Capacitor [capacitance=100nF voltage=35V package="100 mil [THT, multilayer]"]
  C3 = Ceramic Capacitor [capacitance=100nF voltage=35V package="100 mil [THT, multilayer]"]
  R6 = Resistor [tolerance=±5% power=0.25 resistance=50k package=THT]
  C4 = Electrolytic Capacitor [capacitance=1µF voltage=35V package="100 mil [THT, electrolytic]"]
  S1 = Pushbutton [package="[THT]"]
  R7 = Resistor [tolerance=±5% power=0.25 resistance=1M package=THT]

nets:
  N1: U1.DIS, R1.Pin_0, R2.Pin_0
  N2: U1.THR, U1.TRIG, R4.WIPER
  N3: U1.CV, C2.1
  N4: U1.RST, U1.RST2, U1.VCC, R1.Pin_1, R6.Pin_0, S1.Pin_1, S1.Pin_2, R7.Pin_0
  N5: U1.GND, C1.-, C2.0, C3.0, C4.-
  N6: U1.TRIG2, S1.Pin_3, S1.Pin_4, R7.Pin_1
  N7: U1.CV2, C3.1
  N8: U1.THR2, U1.DIS2, R6.Pin_1, C4.+
  N9: R2.Pin_1, C1.+, R4.CCW
