// Logisim project 8BitComp.circ as structural Verilog: 15 circuits, main circuit main
module RegisterThing (
  input  [7:0] BUS_IN,
  input  CLOCK,
  input  LOAD_EN,
  input  BUS_OUT_EN,
  output [7:0] BUS_OUT,
  output [7:0] DATA
);

  Register register_1 (.D(BUS_IN), .en(LOAD_EN), .clk(CLOCK), .Q(DATA));  // open: clr
  assign BUS_OUT = BUS_OUT_EN ? DATA : 8'bz;  // Controlled_Buffer controlled_buffer_1
endmodule

module main (
  input  in_1,
  input  in_2,
  input  in_3,
  input  [7:0] in_4,
  input  in_5
);

  wire ALU_INPUT_MOD, ALU_INVERT_OUT, ALU_REPLACE_B, and_1_out, and_2_out, and_3_out, and_4_out, clock_1_out,
       clock_2_out, clock_3_out, clock_4_out, clock_5_out, clock_6_out, clock_7_out, comparator_1_eq,
       comparator_1_gt, DATA_OUT_DIS, INST_NOT_DONE, JUMP_COND, JUMP_DIS, JUMP_INST, nALU_B_SEL_SYS, nCLOCK,
       nor_1_out, nor_2_out, nor_3_out, nor_4_out, nor_5_out, not_2_out, not_3_out, not_5_out, not_6_out,
       not_7_out, not_10_out, not_11_out, not_12_out, not_13_out, not_14_out, not_15_out, not_16_out,
       not_17_out, not_18_out, not_19_out, not_20_out, not_21_out, RAM_ADDR_FROM_DATA, RAM_IN_DIS,
       RAM_OUT_DIS, RAM_REG_IN_DIS, REG_IN_DIS, REG_OUT_DIS, RegisterLoadSelector_out_0,
       RegisterLoadSelector_out_1, RegisterLoadSelector_out_2, RegisterLoadSelector_out_3,
       RegisterLoadSelector_out_4, registerselector_1_out_0, registerselector_1_out_1,
       registerselector_1_out_2, registerselector_1_out_3, registerselector_1_out_4,
       registerselector_2_out_0, registerselector_2_out_1, registerselector_2_out_2, registerselector_2_out_3;
  wire [1:0] ALU_B_SEL, ALU_SELECT;
  wire [2:0] programrom_1_data, programrom_1_data_2, REG_OUT_SEL, SET_REG_SEL;
  wire [3:0] microcodecounter_1_address;
  wire [6:0] microcoderom_1_io_flags;
  wire [7:0] adder_1_out, ALUOutRegister_data_out, bit_extender_1_out, bit_extender_2_out,
       bit_extender_3_out, bit_extender_4_out, bit_extender_5_out, bit_extender_6_out,
       controlled_buffer_4_out, decoder_1_out0, decoder_2_out0, multiplexer_1_out, multiplexer_4_out,
       multiplexer_5_out, multiplexer_6_out, nand_1_out, not_8_out, not_9_out, programcounter_1_address,
       programcounter_1_bus_out, programrom_1_bus_out, programrom_1_opcode, RealPC_data_out, Reg0_data_out,
       Reg1_data_out, Reg2_data_out, Reg3_data_out, rregister_1_data_out, xor_1_out, xor_2_out, xor_3_out,
       xor_4_out, xor_5_out;
  wire [7:1] Reg4_data_out;

  Clock clock_1 (.out(clock_1_out));
  Clock clock_2 (.out(clock_2_out));
  nor nor_1 (nor_1_out, clock_2_out, INST_NOT_DONE);
  not not_1 (nCLOCK, clock_1_out);
  not not_2 (not_2_out, JUMP_INST);
  not not_3 (not_3_out, JUMP_COND);
  and and_1 (and_1_out, not_2_out, not_3_out);
  not not_4 (JUMP_DIS, and_1_out);
  LedBar OPCODE (
    .led0(programrom_1_opcode[7]), .led1(programrom_1_opcode[6]), .led2(programrom_1_opcode[5]),
    .led3(programrom_1_opcode[4]), .led4(programrom_1_opcode[3]), .led5(programrom_1_opcode[2]),
    .led6(programrom_1_opcode[1]), .led7(programrom_1_opcode[0]));
  LedBar #(.matrixcols(4)) ledbar_1 (
    .led0(microcodecounter_1_address[3]), .led1(microcodecounter_1_address[2]),
    .led2(microcodecounter_1_address[1]), .led3(microcodecounter_1_address[0]));
  Clock clock_3 (.out(clock_3_out));
  LedBar REAL_PC (
    .led0(RealPC_data_out[7]), .led1(RealPC_data_out[6]), .led2(RealPC_data_out[5]),
    .led3(RealPC_data_out[4]), .led4(RealPC_data_out[3]), .led5(RealPC_data_out[2]),
    .led6(RealPC_data_out[1]), .led7(RealPC_data_out[0]));
  RRegister RealPC (
    .LOAD_CLOCK(nor_1_out), .DATA_IN(programcounter_1_address), .RESET_DIS(in_1), .DATA_OUT(RealPC_data_out));
  MicrocodeCounter microcodecounter_1 (
    .CLOCK(nCLOCK), .SYNC_RESET_DIS(INST_NOT_DONE), .ASYNC_RESET_DIS(in_1), .COUNT_EN(INST_NOT_DONE),
    .ADDRESS(microcodecounter_1_address));
  Multiplexer #(.width(8)) multiplexer_1 (
    .in0(rregister_1_data_out), .in1({programrom_1_data_2, ALU_B_SEL, programrom_1_data}),
    .out(multiplexer_1_out), .sel(RAM_ADDR_FROM_DATA));
  Clock clock_4 (.out(clock_4_out));
  not not_5 (not_5_out, INST_NOT_DONE);
  MicrocodeROM microcoderom_1 (
    .OPCODE(programrom_1_opcode), .MICRO_COUNT(microcodecounter_1_address),
    .IO_FLAGS({REG_IN_DIS, microcoderom_1_io_flags[6:4], REG_OUT_DIS, microcoderom_1_io_flags[2:0]}),
    .ALU_FLAGS({INST_NOT_DONE, RAM_ADDR_FROM_DATA, nALU_B_SEL_SYS, ALU_REPLACE_B, ALU_SELECT, ALU_INPUT_MOD, ALU_INVERT_OUT}));
  ProgramCounter programcounter_1 (
    .BUS_IN(programcounter_1_bus_out), .CLOCK(clock_3_out), .RESET_DIS(in_1), .LOAD_DIS(JUMP_DIS),
    .OUTPUT_EN(in_2), .COUNT_EN(not_5_out), .BUS_OUT(programcounter_1_bus_out),
    .ADDRESS(programcounter_1_address));
  RAMThing ramthing_1 (
    .BUS_IN(programcounter_1_bus_out), .ADDRESS(multiplexer_1_out), .CLOCK(clock_4_out), .OUTPUT_EN(in_5),
    .BUS_OUT(programcounter_1_bus_out));  // open: LOAD_EN
  LedBar ledbar_2 (
    .led0(programcounter_1_address[7]), .led1(programcounter_1_address[6]),
    .led2(programcounter_1_address[5]), .led3(programcounter_1_address[4]),
    .led4(programcounter_1_address[3]), .led5(programcounter_1_address[2]),
    .led6(programcounter_1_address[1]), .led7(programcounter_1_address[0]));
  LedBar ALU_FLAGS (
    .led0(INST_NOT_DONE), .led1(RAM_ADDR_FROM_DATA), .led2(nALU_B_SEL_SYS), .led3(ALU_REPLACE_B),
    .led4(ALU_SELECT[1]), .led5(ALU_SELECT[0]), .led6(ALU_INPUT_MOD), .led7(ALU_INVERT_OUT));
  LedBar IO_FLAGS (
    .led0(REG_IN_DIS), .led1(microcoderom_1_io_flags[6]), .led2(microcoderom_1_io_flags[5]),
    .led3(microcoderom_1_io_flags[4]), .led4(REG_OUT_DIS), .led5(microcoderom_1_io_flags[2]),
    .led6(microcoderom_1_io_flags[1]), .led7(microcoderom_1_io_flags[0]));
  ProgramROM programrom_1 (
    .ADDRESS(RealPC_data_out), .DATA_OUT_DIS(DATA_OUT_DIS), .BUS_OUT(programrom_1_bus_out),
    .DATA({programrom_1_data_2, ALU_B_SEL, programrom_1_data}), .OPCODE(programrom_1_opcode));
  LedBar DATA (
    .led0(programrom_1_data_2[2]), .led1(programrom_1_data_2[1]), .led2(programrom_1_data_2[0]),
    .led3(ALU_B_SEL[1]), .led4(ALU_B_SEL[0]), .led5(programrom_1_data[2]), .led6(programrom_1_data[1]),
    .led7(programrom_1_data[0]));
  not not_6 (not_6_out, RAM_REG_IN_DIS);
  and and_2 (and_2_out, not_6_out, clock_5_out);
  Clock clock_5 (.out(clock_5_out));
  assign programcounter_1_bus_out = not_7_out ? programrom_1_bus_out : 8'bz;  // Controlled_Buffer controlled_buffer_1
  not not_7 (not_7_out, DATA_OUT_DIS);
  Decoder #(.select(3)) decoder_1 (
    .out0(decoder_1_out0[0]), .out1(decoder_1_out0[1]), .out2(decoder_1_out0[2]), .out3(decoder_1_out0[3]),
    .out4(decoder_1_out0[4]), .out5(decoder_1_out0[5]), .out6(decoder_1_out0[6]), .out7(decoder_1_out0[7]),
    .sel(microcoderom_1_io_flags[2:0]), .en(REG_OUT_DIS));
  Decoder #(.select(3)) decoder_2 (
    .out0(decoder_2_out0[0]), .out1(decoder_2_out0[1]), .out2(decoder_2_out0[2]), .out3(decoder_2_out0[3]),
    .out4(decoder_2_out0[4]), .out5(decoder_2_out0[5]), .out6(decoder_2_out0[6]), .out7(decoder_2_out0[7]),
    .sel(microcoderom_1_io_flags[6:4]), .en(REG_IN_DIS));
  assign {not_8_out[7:4], RAM_OUT_DIS, not_8_out[2], DATA_OUT_DIS, not_8_out[0]} = ~decoder_1_out0;  // NOT_Gate not_8, 8 bits wide
  and and_3 (and_3_out, microcoderom_1_io_flags[1], microcoderom_1_io_flags[2]);
  assign {not_9_out[7:5], RAM_REG_IN_DIS, RAM_IN_DIS, JUMP_INST, not_9_out[1:0]} = ~decoder_2_out0;  // NOT_Gate not_9, 8 bits wide
  RRegister rregister_1 (
    .LOAD_CLOCK(and_2_out), .DATA_IN(programcounter_1_bus_out), .RESET_DIS(in_1),
    .DATA_OUT(rregister_1_data_out));
  LedBar #(.matrixcols(3)) ledbar_3 (.led0(REG_OUT_SEL[2]), .led1(REG_OUT_SEL[1]), .led2(REG_OUT_SEL[0]));
  Multiplexer #(.width(3)) multiplexer_2 (
    .in0(microcoderom_1_io_flags[2:0]), .in1(programrom_1_data), .out(REG_OUT_SEL), .sel(and_3_out));
  and and_4 (and_4_out, microcoderom_1_io_flags[5], microcoderom_1_io_flags[6]);
  LedBar #(.matrixcols(3)) ledbar_4 (.led0(SET_REG_SEL[2]), .led1(SET_REG_SEL[1]), .led2(SET_REG_SEL[0]));
  Multiplexer #(.width(3)) multiplexer_3 (
    .in0(microcoderom_1_io_flags[6:4]), .in1(programrom_1_data_2), .out(SET_REG_SEL), .sel(and_4_out));
  LedBar ledbar_5 (
    .led0(programcounter_1_bus_out[7]), .led1(programcounter_1_bus_out[6]),
    .led2(programcounter_1_bus_out[5]), .led3(programcounter_1_bus_out[4]),
    .led4(programcounter_1_bus_out[3]), .led5(programcounter_1_bus_out[2]),
    .led6(programcounter_1_bus_out[1]), .led7(programcounter_1_bus_out[0]));
  Pull_Resistor pull_resistor_1 (.node(programcounter_1_bus_out[7]));
  Pull_Resistor pull_resistor_2 (.node(programcounter_1_bus_out[6]));
  Pull_Resistor pull_resistor_3 (.node(programcounter_1_bus_out[5]));
  Pull_Resistor pull_resistor_4 (.node(programcounter_1_bus_out[4]));
  Pull_Resistor pull_resistor_5 (.node(programcounter_1_bus_out[3]));
  Pull_Resistor pull_resistor_6 (.node(programcounter_1_bus_out[2]));
  Pull_Resistor pull_resistor_7 (.node(programcounter_1_bus_out[1]));
  Pull_Resistor pull_resistor_8 (.node(programcounter_1_bus_out[0]));
  assign programcounter_1_bus_out = in_3 ? in_4 : 8'bz;  // Controlled_Buffer controlled_buffer_2
  RRegister Reg0 (
    .LOAD_CLOCK(RegisterLoadSelector_out_0), .DATA_IN(ALUOutRegister_data_out), .RESET_DIS(in_1),
    .DATA_OUT(Reg0_data_out));
  not not_10 (not_10_out, registerselector_1_out_0);
  assign programcounter_1_bus_out = not_10_out ? Reg0_data_out : 8'bz;  // Controlled_Buffer controlled_buffer_3
  LedBar ledbar_6 (
    .led0(Reg0_data_out[7]), .led1(Reg0_data_out[6]), .led2(Reg0_data_out[5]), .led3(Reg0_data_out[4]),
    .led4(Reg0_data_out[3]), .led5(Reg0_data_out[2]), .led6(Reg0_data_out[1]), .led7(Reg0_data_out[0]));
  not not_11 (not_11_out, registerselector_2_out_0);
  assign controlled_buffer_4_out = not_11_out ? Reg0_data_out : 8'bz;  // Controlled_Buffer controlled_buffer_4
  LedBar ledbar_7 (
    .led0(controlled_buffer_4_out[7]), .led1(controlled_buffer_4_out[6]), .led2(controlled_buffer_4_out[5]),
    .led3(controlled_buffer_4_out[4]), .led4(controlled_buffer_4_out[3]), .led5(controlled_buffer_4_out[2]),
    .led6(controlled_buffer_4_out[1]), .led7(controlled_buffer_4_out[0]));
  nor nor_2 (nor_2_out, ALU_INPUT_MOD, ALU_INPUT_MOD);
  Multiplexer #(.width(8)) multiplexer_4 (
    .in0(controlled_buffer_4_out), .in1({8{1'b1}}), .out(multiplexer_4_out), .sel(ALU_REPLACE_B));
  nor nor_3 (nor_3_out, ALU_INVERT_OUT, ALU_INVERT_OUT);
  assign bit_extender_1_out = {{7{nor_4_out}}, nor_4_out};  // Bit_Extender bit_extender_1
  nor nor_4 (nor_4_out, nor_2_out, ALU_REPLACE_B);
  assign bit_extender_2_out = {{7{ALU_INPUT_MOD}}, ALU_INPUT_MOD};  // Bit_Extender bit_extender_2
  assign bit_extender_3_out = {{7{nor_5_out}}, nor_5_out};  // Bit_Extender bit_extender_3
  nor nor_5 (nor_5_out, nor_3_out, ALU_INPUT_MOD);
  assign xor_1_out = programcounter_1_bus_out ^ bit_extender_1_out;  // XOR_Gate xor_1, 8 bits wide
  assign xor_2_out = multiplexer_4_out ^ bit_extender_2_out;  // XOR_Gate xor_2, 8 bits wide
  assign xor_3_out = programcounter_1_bus_out ^ bit_extender_3_out;  // XOR_Gate xor_3, 8 bits wide
  RRegister Reg1 (
    .LOAD_CLOCK(RegisterLoadSelector_out_1), .DATA_IN(ALUOutRegister_data_out), .RESET_DIS(in_1),
    .DATA_OUT(Reg1_data_out));
  not not_12 (not_12_out, registerselector_1_out_1);
  assign programcounter_1_bus_out = not_12_out ? Reg1_data_out : 8'bz;  // Controlled_Buffer controlled_buffer_5
  LedBar ledbar_8 (
    .led0(Reg1_data_out[7]), .led1(Reg1_data_out[6]), .led2(Reg1_data_out[5]), .led3(Reg1_data_out[4]),
    .led4(Reg1_data_out[3]), .led5(Reg1_data_out[2]), .led6(Reg1_data_out[1]), .led7(Reg1_data_out[0]));
  not not_13 (not_13_out, registerselector_2_out_1);
  assign controlled_buffer_4_out = not_13_out ? Reg1_data_out : 8'bz;  // Controlled_Buffer controlled_buffer_6
  not not_14 (not_14_out, comparator_1_gt);
  not not_15 (not_15_out, comparator_1_eq);
  Comparator #(.mode("unsigned")) comparator_1 (
    .a(xor_1_out), .b(xor_2_out), .gt(comparator_1_gt), .eq(comparator_1_eq));  // open: lt
  assign bit_extender_4_out = {{7{not_14_out}}, not_14_out};  // Bit_Extender bit_extender_4
  assign bit_extender_5_out = {{7{not_15_out}}, not_15_out};  // Bit_Extender bit_extender_5
  Adder adder_1 (.a(xor_3_out), .b(xor_2_out), .out(adder_1_out));  // open: cin, cout
  assign xor_4_out = programcounter_1_bus_out ^ controlled_buffer_4_out;  // XOR_Gate xor_4, 8 bits wide
  Multiplexer #(.width(8)) multiplexer_5 (
    .in0(xor_4_out), .in1({1'b0, programcounter_1_bus_out[7:1]}), .out(multiplexer_5_out), .sel(ALU_INPUT_MOD));
  LedBar ledbar_9 (
    .led0(adder_1_out[7]), .led1(adder_1_out[6]), .led2(adder_1_out[5]), .led3(adder_1_out[4]),
    .led4(adder_1_out[3]), .led5(adder_1_out[2]), .led6(adder_1_out[1]), .led7(adder_1_out[0]));
  RRegister Reg2 (
    .LOAD_CLOCK(RegisterLoadSelector_out_2), .DATA_IN(ALUOutRegister_data_out), .RESET_DIS(in_1),
    .DATA_OUT(Reg2_data_out));
  not not_16 (not_16_out, registerselector_1_out_2);
  assign programcounter_1_bus_out = not_16_out ? Reg2_data_out : 8'bz;  // Controlled_Buffer controlled_buffer_7
  LedBar ledbar_10 (
    .led0(Reg2_data_out[7]), .led1(Reg2_data_out[6]), .led2(Reg2_data_out[5]), .led3(Reg2_data_out[4]),
    .led4(Reg2_data_out[3]), .led5(Reg2_data_out[2]), .led6(Reg2_data_out[1]), .led7(Reg2_data_out[0]));
  not not_17 (not_17_out, registerselector_2_out_2);
  assign controlled_buffer_4_out = not_17_out ? Reg2_data_out : 8'bz;  // Controlled_Buffer controlled_buffer_8
  assign nand_1_out = ~(xor_1_out & xor_2_out);  // NAND_Gate nand_1, 8 bits wide
  Multiplexer #(.select(3), .width(8)) multiplexer_6 (
    .in0(adder_1_out), .in1(bit_extender_4_out), .in2(bit_extender_5_out), .in3(nand_1_out),
    .in4(bit_extender_5_out), .in5(bit_extender_4_out), .in6(adder_1_out), .in7(multiplexer_5_out),
    .out(multiplexer_6_out), .sel({ALU_REPLACE_B, ALU_SELECT}));
  RRegister Reg3 (
    .LOAD_CLOCK(RegisterLoadSelector_out_3), .DATA_IN(ALUOutRegister_data_out), .RESET_DIS(in_1),
    .DATA_OUT(Reg3_data_out));
  not not_18 (not_18_out, registerselector_1_out_3);
  assign programcounter_1_bus_out = not_18_out ? Reg3_data_out : 8'bz;  // Controlled_Buffer controlled_buffer_9
  not not_19 (not_19_out, registerselector_2_out_3);
  assign controlled_buffer_4_out = not_19_out ? Reg3_data_out : 8'bz;  // Controlled_Buffer controlled_buffer_10
  LedBar ledbar_11 (
    .led0(Reg3_data_out[7]), .led1(Reg3_data_out[6]), .led2(Reg3_data_out[5]), .led3(Reg3_data_out[4]),
    .led4(Reg3_data_out[3]), .led5(Reg3_data_out[2]), .led6(Reg3_data_out[1]), .led7(Reg3_data_out[0]));
  assign bit_extender_6_out = {{7{ALU_INVERT_OUT}}, ALU_INVERT_OUT};  // Bit_Extender bit_extender_6
  RRegister Reg4 (
    .LOAD_CLOCK(RegisterLoadSelector_out_4), .DATA_IN(ALUOutRegister_data_out), .RESET_DIS(in_1),
    .DATA_OUT({Reg4_data_out, JUMP_COND}));
  not not_20 (not_20_out, registerselector_1_out_4);
  assign programcounter_1_bus_out = not_20_out ? {Reg4_data_out, JUMP_COND} : 8'bz;  // Controlled_Buffer controlled_buffer_11
  not not_21 (not_21_out, nALU_B_SEL_SYS);
  assign controlled_buffer_4_out = not_21_out ? {Reg4_data_out, JUMP_COND} : 8'bz;  // Controlled_Buffer controlled_buffer_12
  LedBar ledbar_12 (
    .led0(xor_5_out[7]), .led1(xor_5_out[6]), .led2(xor_5_out[5]), .led3(xor_5_out[4]), .led4(xor_5_out[3]),
    .led5(xor_5_out[2]), .led6(xor_5_out[1]), .led7(xor_5_out[0]));
  assign xor_5_out = bit_extender_6_out ^ multiplexer_6_out;  // XOR_Gate xor_5, 8 bits wide
  LedBar ledbar_13 (
    .led0(Reg4_data_out[7]), .led1(Reg4_data_out[6]), .led2(Reg4_data_out[5]), .led3(Reg4_data_out[4]),
    .led4(Reg4_data_out[3]), .led5(Reg4_data_out[2]), .led6(Reg4_data_out[1]), .led7(JUMP_COND));
  Clock clock_6 (.out(clock_6_out));
  Clock clock_7 (.out(clock_7_out));
  RegisterSelector RegisterLoadSelector (
    .A(SET_REG_SEL[0]), .B(SET_REG_SEL[1]), .C(SET_REG_SEL[2]), .EN_OUT_1(clock_6_out),
    .DIS_OUT_2(REG_IN_DIS), .DIS_OUT_3(1'b0), .OUT_0(RegisterLoadSelector_out_0),
    .OUT_1(RegisterLoadSelector_out_1), .OUT_2(RegisterLoadSelector_out_2),
    .OUT_3(RegisterLoadSelector_out_3), .OUT_4(RegisterLoadSelector_out_4));  // open: OUT_5, OUT_6, OUT_7
  RegisterSelector registerselector_1 (
    .A(REG_OUT_SEL[0]), .B(REG_OUT_SEL[1]), .C(REG_OUT_SEL[2]), .EN_OUT_1(1'b1), .DIS_OUT_2(1'b0),
    .DIS_OUT_3(REG_OUT_DIS), .OUT_0(registerselector_1_out_0), .OUT_1(registerselector_1_out_1),
    .OUT_2(registerselector_1_out_2), .OUT_3(registerselector_1_out_3), .OUT_4(registerselector_1_out_4));  // open: OUT_5, OUT_6, OUT_7
  RegisterSelector registerselector_2 (
    .A(ALU_B_SEL[0]), .B(ALU_B_SEL[1]), .C(1'b0), .EN_OUT_1(nALU_B_SEL_SYS), .DIS_OUT_2(1'b0),
    .DIS_OUT_3(1'b0), .OUT_0(registerselector_2_out_0), .OUT_1(registerselector_2_out_1),
    .OUT_2(registerselector_2_out_2), .OUT_3(registerselector_2_out_3));  // open: OUT_4, OUT_5, OUT_6, OUT_7
  RRegister ALUOutRegister (
    .LOAD_CLOCK(clock_7_out), .DATA_IN(xor_5_out), .RESET_DIS(in_1), .DATA_OUT(ALUOutRegister_data_out));
  LedBar ledbar_14 (
    .led0(ALUOutRegister_data_out[7]), .led1(ALUOutRegister_data_out[6]), .led2(ALUOutRegister_data_out[5]),
    .led3(ALUOutRegister_data_out[4]), .led4(ALUOutRegister_data_out[3]), .led5(ALUOutRegister_data_out[2]),
    .led6(ALUOutRegister_data_out[1]), .led7(ALUOutRegister_data_out[0]));

  // Other names for the same wires on the sheet: ALU_SELECT[2] = ALU_REPLACE_B; MASTER_RESET_DIS = in_1
endmodule

module ProgramCounter (
  input  [7:0] BUS_IN,
  input  CLOCK,
  input  RESET_DIS,
  input  LOAD_DIS,
  input  OUTPUT_EN,
  input  COUNT_EN,
  output [7:0] BUS_OUT,
  output [7:0] ADDRESS
);

  wire n74161_1_pin15;

  _74161 u_74161_1 (
    .pin1(RESET_DIS), .pin2(CLOCK), .pin3(BUS_IN[0]), .pin4(BUS_IN[1]), .pin5(BUS_IN[2]), .pin6(BUS_IN[3]),
    .pin7(COUNT_EN), .pin15(n74161_1_pin15), .pin14(ADDRESS[0]), .pin13(ADDRESS[1]), .pin12(ADDRESS[2]),
    .pin11(ADDRESS[3]), .pin10(COUNT_EN), .pin9(LOAD_DIS));
  _74161 u_74161_2 (
    .pin1(RESET_DIS), .pin2(CLOCK), .pin3(BUS_IN[4]), .pin4(BUS_IN[5]), .pin5(BUS_IN[6]), .pin6(BUS_IN[7]),
    .pin7(n74161_1_pin15), .pin14(ADDRESS[4]), .pin13(ADDRESS[5]), .pin12(ADDRESS[6]), .pin11(ADDRESS[7]),
    .pin10(n74161_1_pin15), .pin9(LOAD_DIS));  // open: pin15
  assign BUS_OUT = OUTPUT_EN ? ADDRESS : 8'bz;  // Controlled_Buffer controlled_buffer_1
endmodule

module ALU (
  input  [7:0] OP,
  input  [7:0] REG_A,
  input  [7:0] REG_B,
  input  OUTPUT_EN,
  output [7:0] BUS_OUT
);

  wire [7:0] adder_1_out, multiplexer_1_out, subtractor_1_out;

  Adder adder_1 (.a(REG_A), .b(REG_B), .out(adder_1_out));  // open: cin, cout
  Subtractor subtractor_1 (.a(REG_A), .b(REG_B), .out(subtractor_1_out));  // open: bin, bout
  Multiplexer #(.width(8)) multiplexer_1 (
    .in0(adder_1_out), .in1(subtractor_1_out), .out(multiplexer_1_out), .sel(OP[0]));
  assign BUS_OUT = OUTPUT_EN ? multiplexer_1_out : 8'bz;  // Controlled_Buffer controlled_buffer_1
endmodule

module ProgramROM (
  input  [7:0] ADDRESS,
  input  DATA_OUT_DIS,
  output [7:0] BUS_OUT,
  output [7:0] DATA,
  output [7:0] OPCODE
);

  wire not_1_out;

  ROM rom_1 (.addr(ADDRESS), .data(OPCODE));
  not not_1 (not_1_out, DATA_OUT_DIS);
  ROM rom_2 (.addr(ADDRESS), .data(DATA));
  assign BUS_OUT = not_1_out ? DATA : 8'bz;  // Controlled_Buffer controlled_buffer_1

  // Notes on the sheet:
  //   contents of rom_1 (hex, n*v repeats v):
  //   0 31 1 3c c 42
  //   contents of rom_2 (hex, n*v repeats v):
  //   1 2 41 62 0 4
endmodule

module FlagsMicrocodeROM (
  input  [7:0] OPCODE,
  input  [3:0] MICRO_COUNT,
  output [7:0] BUS_IN_FLAGS,
  output [7:0] BUS_OUT_FLAGS,
  output OUT_0,
  output OUT_1
);

  wire [7:2] rom_1_data;

  ROM #(.addrWidth(11)) rom_1 (.addr({OPCODE[6:0], MICRO_COUNT}), .data({rom_1_data, OUT_1, OUT_0}));
  Decoder #(.select(3)) decoder_1 (
    .out0(BUS_IN_FLAGS[0]), .out1(BUS_IN_FLAGS[1]), .out2(BUS_IN_FLAGS[2]), .out3(BUS_IN_FLAGS[3]),
    .out4(BUS_IN_FLAGS[4]), .out5(BUS_IN_FLAGS[5]), .out6(BUS_IN_FLAGS[6]), .out7(BUS_IN_FLAGS[7]),
    .sel(rom_1_data[7:5]));  // open: en
  Decoder #(.select(3)) decoder_2 (
    .out0(BUS_OUT_FLAGS[0]), .out1(BUS_OUT_FLAGS[1]), .out2(BUS_OUT_FLAGS[2]), .out3(BUS_OUT_FLAGS[3]),
    .out4(BUS_OUT_FLAGS[4]), .out5(BUS_OUT_FLAGS[5]), .out6(BUS_OUT_FLAGS[6]), .out7(BUS_OUT_FLAGS[7]),
    .sel(rom_1_data[4:2]));  // open: en

  // Notes on the sheet:
  //   contents of rom_1 (hex, n*v repeats v):
  //   16*0 2 15*ff 2 15*ff 2 15*ff 2 15*ff 29 29 1966*ff
endmodule

module RAMThing (
  input  [7:0] BUS_IN,
  input  [7:0] ADDRESS,
  input  CLOCK,
  input  LOAD_EN,
  input  OUTPUT_EN,
  output [7:0] BUS_OUT
);
endmodule

module MicrocodeCounter (
  input  CLOCK,
  input  SYNC_RESET_DIS,
  input  ASYNC_RESET_DIS,
  input  COUNT_EN,
  output [3:0] ADDRESS
);

  wire n74161_1_pin3;

  _74161 u_74161_1 (
    .pin1(ASYNC_RESET_DIS), .pin2(CLOCK), .pin3(n74161_1_pin3), .pin4(n74161_1_pin3), .pin5(n74161_1_pin3),
    .pin6(n74161_1_pin3), .pin7(COUNT_EN), .pin14(ADDRESS[0]), .pin13(ADDRESS[1]), .pin12(ADDRESS[2]),
    .pin11(ADDRESS[3]), .pin10(COUNT_EN), .pin9(SYNC_RESET_DIS));  // open: pin15
  // also tied to GND on the sheet: n74161_1_pin3
endmodule

module PlusOne (
  input  [7:0] VAL_IN,
  input  OUTPUT_EN,
  output [7:0] VAL_OUT
);

  wire [7:0] adder_1_out;

  Adder adder_1 (.a(VAL_IN), .b(8'h1), .out(adder_1_out));  // open: cin, cout
  assign VAL_OUT = OUTPUT_EN ? adder_1_out : 8'bz;  // Controlled_Buffer controlled_buffer_1
endmodule

module StackPointer (
  input  CLOCK,
  input  PUSH_EN,
  input  POP_EN,
  output out_4
);

  _74283 u_74283_1 ();  // open: pin1, pin2, pin3, pin4, pin5, pin6, pin7, pin15, pin14, pin13, pin12, pin11, pin10, pin9
  _74161 u_74161_1 ();  // open: pin1, pin2, pin3, pin4, pin5, pin6, pin7, pin15, pin14, pin13, pin12, pin11, pin10, pin9
endmodule

module RLRegister (
  input  CLOCK,
  input  [7:0] DATA_IN,
  input  LOAD_DIS,
  input  RESET_EN,
  input  OUTPUT_DIS,
  output [7:0] DATA_OUT
);

  wire and_1_out, not_1_out, not_2_out;
  wire [7:0] n74273_1_pin2;

  and and_1 (and_1_out, ~LOAD_DIS, CLOCK);  // AND_Gate
  not not_1 (not_1_out, RESET_EN);
  not not_2 (not_2_out, OUTPUT_DIS);
  _74273 u_74273_1 (
    .pin1(not_1_out), .pin2(n74273_1_pin2[0]), .pin3(DATA_IN[0]), .pin4(DATA_IN[1]), .pin5(n74273_1_pin2[1]),
    .pin6(n74273_1_pin2[2]), .pin7(DATA_IN[2]), .pin8(DATA_IN[3]), .pin9(n74273_1_pin2[3]),
    .pin19(n74273_1_pin2[7]), .pin18(DATA_IN[7]), .pin17(DATA_IN[6]), .pin16(n74273_1_pin2[6]),
    .pin15(n74273_1_pin2[5]), .pin14(DATA_IN[5]), .pin13(DATA_IN[4]), .pin12(n74273_1_pin2[4]),
    .pin11(and_1_out));
  assign DATA_OUT = not_2_out ? n74273_1_pin2 : 8'bz;  // Controlled_Buffer controlled_buffer_1
endmodule

module RRegister (
  input  LOAD_CLOCK,
  input  [7:0] DATA_IN,
  input  RESET_DIS,
  output [7:0] DATA_OUT
);

  _74273 u_74273_1 (
    .pin1(RESET_DIS), .pin2(DATA_OUT[0]), .pin3(DATA_IN[0]), .pin4(DATA_IN[1]), .pin5(DATA_OUT[1]),
    .pin6(DATA_OUT[2]), .pin7(DATA_IN[2]), .pin8(DATA_IN[3]), .pin9(DATA_OUT[3]), .pin19(DATA_OUT[7]),
    .pin18(DATA_IN[7]), .pin17(DATA_IN[6]), .pin16(DATA_OUT[6]), .pin15(DATA_OUT[5]), .pin14(DATA_IN[5]),
    .pin13(DATA_IN[4]), .pin12(DATA_OUT[4]), .pin11(LOAD_CLOCK));
endmodule

module RegisterSelector (
  input  A,
  input  B,
  input  C,
  input  EN_OUT_1,
  input  DIS_OUT_2,
  input  DIS_OUT_3,
  output OUT_0,
  output OUT_1,
  output OUT_2,
  output OUT_3,
  output OUT_4,
  output OUT_5,
  output OUT_6,
  output OUT_7
);

  wire and_1_out;
  wire [7:0] decoder_1_out0;

  and and_1 (and_1_out, EN_OUT_1, ~DIS_OUT_2, ~DIS_OUT_3);  // AND_Gate
  Decoder #(.select(3)) decoder_1 (
    .out0(decoder_1_out0[0]), .out1(decoder_1_out0[1]), .out2(decoder_1_out0[2]), .out3(decoder_1_out0[3]),
    .out4(decoder_1_out0[4]), .out5(decoder_1_out0[5]), .out6(decoder_1_out0[6]), .out7(decoder_1_out0[7]),
    .sel({C, B, A}), .en(and_1_out));
  assign {OUT_7, OUT_6, OUT_5, OUT_4, OUT_3, OUT_2, OUT_1, OUT_0} = ~decoder_1_out0;  // NOT_Gate not_1, 8 bits wide
endmodule

module ALUROM (
  input  [7:0] OPCODE,
  input  [3:0] MICRO_COUNT,
  output [7:0] DATA
);

  ROM #(.addrWidth(11)) rom_1 (.addr({OPCODE[6:0], MICRO_COUNT}), .data(DATA));

  // Notes on the sheet:
  //   contents of rom_1 (hex, n*v repeats v):
  //   16*0 7a 15*ff 2 15*ff 2 15*ff 2 15*ff 29 29 1966*ff
endmodule

module MicrocodeROM (
  input  [7:0] OPCODE,
  input  [3:0] MICRO_COUNT,
  output [7:0] IO_FLAGS,
  output [7:0] ALU_FLAGS
);

  ROM #(.addrWidth(11)) rom_1 (.addr({OPCODE[6:0], MICRO_COUNT}), .data(IO_FLAGS));
  ROM #(.addrWidth(11)) rom_2 (.addr({OPCODE[6:0], MICRO_COUNT}), .data(ALU_FLAGS));

  // Notes on the sheet:
  //   contents of rom_1 (hex, n*v repeats v):
  //   16*0 77 175*ff 77 15*ff 77 559*ff 9 15*ff 19 15*ff 29 15*ff 39 143*ff 77 63*ff 44 a9 30*ff a9 991*ff
  //   contents of rom_2 (hex, n*v repeats v):
  //   7*80 0 8*80 60 175*ff 19 15*ff 18 559*ff 7a 15*ff 7a 15*ff 7a 15*ff 7a 143*ff 7a 63*ff 9c 40 30*ff
  //   40 991*ff
endmodule
