// Logisim project 8BitCompALUTest.circ as structural Verilog: 14 circuits, main circuit main
module RegisterThing (
  input  [7:0] BUS_IN,
  input  CLOCK,
  input  LOAD_EN,
  input  BUS_OUT_EN,
  output [7:0] BUS_OUT,
  output [7:0] DATA
);

  Register register_1 (.D(BUS_IN), .en(LOAD_EN), .clk(CLOCK), .Q(DATA));  // open: clr
  assign BUS_OUT = BUS_OUT_EN ? DATA : 8'bz;  // Controlled_Buffer controlled_buffer_1
endmodule

module main (
  input  in_1,
  input  [7:0] A,
  input  in_3,
  input  [2:0] in_4,
  input  [7:0] B
);

  wire comparator_1_eq, comparator_1_gt, nor_1_out, nor_2_out, nor_3_out, nor_4_out, not_1_out, not_2_out;
  wire [7:0] adder_1_out, bit_extender_1_out, bit_extender_2_out, bit_extender_3_out, bit_extender_4_out,
       bit_extender_5_out, bit_extender_6_out, multiplexer_1_out, multiplexer_2_out, multiplexer_3_out,
       nand_1_out, xor_1_out, xor_2_out, xor_3_out, xor_4_out, xor_5_out;

  nor nor_1 (nor_1_out, in_1, in_1);
  Multiplexer #(.width(8)) multiplexer_1 (.in0(B), .in1({8{1'b1}}), .out(multiplexer_1_out), .sel(in_4[2]));
  nor nor_2 (nor_2_out, in_3, in_3);
  assign bit_extender_1_out = {{7{nor_3_out}}, nor_3_out};  // Bit_Extender bit_extender_1
  nor nor_3 (nor_3_out, nor_1_out, in_4[2]);
  assign bit_extender_2_out = {{7{in_1}}, in_1};  // Bit_Extender bit_extender_2
  assign bit_extender_3_out = {{7{nor_4_out}}, nor_4_out};  // Bit_Extender bit_extender_3
  nor nor_4 (nor_4_out, nor_2_out, in_1);
  assign xor_1_out = A ^ bit_extender_1_out;  // XOR_Gate xor_1, 8 bits wide
  assign xor_2_out = multiplexer_1_out ^ bit_extender_2_out;  // XOR_Gate xor_2, 8 bits wide
  assign xor_3_out = A ^ bit_extender_3_out;  // XOR_Gate xor_3, 8 bits wide
  not not_1 (not_1_out, comparator_1_gt);
  not not_2 (not_2_out, comparator_1_eq);
  Comparator #(.mode("unsigned")) comparator_1 (
    .a(xor_1_out), .b(xor_2_out), .gt(comparator_1_gt), .eq(comparator_1_eq));  // open: lt
  assign bit_extender_4_out = {{7{not_1_out}}, not_1_out};  // Bit_Extender bit_extender_4
  assign bit_extender_5_out = {{7{not_2_out}}, not_2_out};  // Bit_Extender bit_extender_5
  Adder adder_1 (.a(xor_3_out), .b(xor_2_out), .out(adder_1_out));  // open: cin, cout
  assign xor_4_out = A ^ B;  // XOR_Gate xor_4, 8 bits wide
  Multiplexer #(.width(8)) multiplexer_2 (.in0(xor_4_out), .in1({1'b0, A[7:1]}), .out(multiplexer_2_out), .sel(in_1));
  LedBar ledbar_1 (
    .led0(adder_1_out[7]), .led1(adder_1_out[6]), .led2(adder_1_out[5]), .led3(adder_1_out[4]),
    .led4(adder_1_out[3]), .led5(adder_1_out[2]), .led6(adder_1_out[1]), .led7(adder_1_out[0]));
  assign nand_1_out = ~(xor_1_out & xor_2_out);  // NAND_Gate nand_1, 8 bits wide
  Multiplexer #(.select(3), .width(8)) multiplexer_3 (
    .in0(adder_1_out), .in1(bit_extender_4_out), .in2(bit_extender_5_out), .in3(nand_1_out),
    .in4(bit_extender_5_out), .in5(bit_extender_4_out), .in6(adder_1_out), .in7(multiplexer_2_out),
    .out(multiplexer_3_out), .sel(in_4));
  assign bit_extender_6_out = {{7{in_3}}, in_3};  // Bit_Extender bit_extender_6
  LedBar ledbar_2 (
    .led0(xor_5_out[7]), .led1(xor_5_out[6]), .led2(xor_5_out[5]), .led3(xor_5_out[4]), .led4(xor_5_out[3]),
    .led5(xor_5_out[2]), .led6(xor_5_out[1]), .led7(xor_5_out[0]));
  assign xor_5_out = bit_extender_6_out ^ multiplexer_3_out;  // XOR_Gate xor_5, 8 bits wide

  // Other names for the same wires on the sheet: ALU_INPUT_MOD = in_1; ALU_INVERT_OUT = in_3; ALU_SELECT[2:0] = in_4;
  //   ALU_REPLACE_B = in_4[2]
endmodule

module ProgramCounter (
  input  [7:0] BUS_IN,
  input  CLOCK,
  input  RESET_DIS,
  input  LOAD_DIS,
  input  OUTPUT_EN,
  input  COUNT_EN,
  output [7:0] BUS_OUT,
  output [7:0] ADDRESS
);

  wire n74161_1_pin15;

  _74161 u_74161_1 (
    .pin1(RESET_DIS), .pin2(CLOCK), .pin3(BUS_IN[0]), .pin4(BUS_IN[1]), .pin5(BUS_IN[2]), .pin6(BUS_IN[3]),
    .pin7(COUNT_EN), .pin15(n74161_1_pin15), .pin14(ADDRESS[0]), .pin13(ADDRESS[1]), .pin12(ADDRESS[2]),
    .pin11(ADDRESS[3]), .pin10(COUNT_EN), .pin9(LOAD_DIS));
  _74161 u_74161_2 (
    .pin1(RESET_DIS), .pin2(CLOCK), .pin3(BUS_IN[4]), .pin4(BUS_IN[5]), .pin5(BUS_IN[6]), .pin6(BUS_IN[7]),
    .pin7(n74161_1_pin15), .pin14(ADDRESS[4]), .pin13(ADDRESS[5]), .pin12(ADDRESS[6]), .pin11(ADDRESS[7]),
    .pin10(n74161_1_pin15), .pin9(LOAD_DIS));  // open: pin15
  assign BUS_OUT = OUTPUT_EN ? ADDRESS : 8'bz;  // Controlled_Buffer controlled_buffer_1
endmodule

module ALU (
  input  [7:0] OP,
  input  [7:0] REG_A,
  input  [7:0] REG_B,
  input  OUTPUT_EN,
  output [7:0] BUS_OUT
);

  wire [7:0] adder_1_out, multiplexer_1_out, subtractor_1_out;

  Adder adder_1 (.a(REG_A), .b(REG_B), .out(adder_1_out));  // open: cin, cout
  Subtractor subtractor_1 (.a(REG_A), .b(REG_B), .out(subtractor_1_out));  // open: bin, bout
  Multiplexer #(.width(8)) multiplexer_1 (
    .in0(adder_1_out), .in1(subtractor_1_out), .out(multiplexer_1_out), .sel(OP[0]));
  assign BUS_OUT = OUTPUT_EN ? multiplexer_1_out : 8'bz;  // Controlled_Buffer controlled_buffer_1
endmodule

module ProgramROM (
  input  [7:0] ADDRESS,
  input  DATA_OUT_DIS,
  output [7:0] BUS_OUT,
  output [7:0] DATA,
  output [7:0] OPCODE
);

  wire not_1_out;

  ROM rom_1 (.addr({ADDRESS[6:0], 1'b0}), .data(OPCODE));
  not not_1 (not_1_out, DATA_OUT_DIS);
  ROM rom_2 (.addr({ADDRESS[6:0], 1'b1}), .data(DATA));
  assign BUS_OUT = not_1_out ? DATA : 8'bz;  // Controlled_Buffer controlled_buffer_1

  // Notes on the sheet:
  //   contents of rom_1 (hex, n*v repeats v):
  //   1 1 2 2 3 3 4 4 5 1 6 6
  //   contents of rom_2 (hex, n*v repeats v):
  //   1 1 2 2 3 3 4 4 5 1 6 6
endmodule

module FlagsMicrocodeROM (
  input  [7:0] OPCODE,
  input  [3:0] MICRO_COUNT,
  output [7:0] BUS_IN_FLAGS,
  output [7:0] BUS_OUT_FLAGS,
  output OUT_0,
  output OUT_1
);

  wire [7:2] rom_1_data;

  ROM #(.addrWidth(11)) rom_1 (.addr({OPCODE[6:0], MICRO_COUNT}), .data({rom_1_data, OUT_1, OUT_0}));
  Decoder #(.select(3)) decoder_1 (
    .out0(BUS_IN_FLAGS[0]), .out1(BUS_IN_FLAGS[1]), .out2(BUS_IN_FLAGS[2]), .out3(BUS_IN_FLAGS[3]),
    .out4(BUS_IN_FLAGS[4]), .out5(BUS_IN_FLAGS[5]), .out6(BUS_IN_FLAGS[6]), .out7(BUS_IN_FLAGS[7]),
    .sel(rom_1_data[7:5]));  // open: en
  Decoder #(.select(3)) decoder_2 (
    .out0(BUS_OUT_FLAGS[0]), .out1(BUS_OUT_FLAGS[1]), .out2(BUS_OUT_FLAGS[2]), .out3(BUS_OUT_FLAGS[3]),
    .out4(BUS_OUT_FLAGS[4]), .out5(BUS_OUT_FLAGS[5]), .out6(BUS_OUT_FLAGS[6]), .out7(BUS_OUT_FLAGS[7]),
    .sel(rom_1_data[4:2]));  // open: en

  // Notes on the sheet:
  //   contents of rom_1 (hex, n*v repeats v):
  //   16*0 2 15*ff 2 15*ff 2 15*ff 2 15*ff 29 29 1966*ff
endmodule

module RAMThing (
  input  [7:0] BUS_IN,
  input  [7:0] ADDRESS,
  input  CLOCK,
  input  LOAD_EN,
  input  OUTPUT_EN,
  output [7:0] BUS_OUT
);
endmodule

module MicrocodeCounter (
  input  CLOCK,
  input  RESET_DIS,
  input  COUNT_EN,
  output [3:0] ADDRESS
);

  wire n74161_1_pin9;

  _74161 u_74161_1 (
    .pin1(RESET_DIS), .pin2(CLOCK), .pin7(COUNT_EN), .pin14(ADDRESS[0]), .pin13(ADDRESS[1]),
    .pin12(ADDRESS[2]), .pin11(ADDRESS[3]), .pin10(COUNT_EN), .pin9(n74161_1_pin9));  // open: pin3, pin4, pin5, pin6, pin15
  // also tied to VCC on the sheet: n74161_1_pin9
endmodule

module PlusOne (
  input  [7:0] VAL_IN,
  input  OUTPUT_EN,
  output [7:0] VAL_OUT
);

  wire [7:0] adder_1_out;

  Adder adder_1 (.a(VAL_IN), .b(8'h1), .out(adder_1_out));  // open: cin, cout
  assign VAL_OUT = OUTPUT_EN ? adder_1_out : 8'bz;  // Controlled_Buffer controlled_buffer_1
endmodule

module StackPointer (
  input  CLOCK,
  input  PUSH_EN,
  input  POP_EN,
  output out_4
);

  _74283 u_74283_1 ();  // open: pin1, pin2, pin3, pin4, pin5, pin6, pin7, pin15, pin14, pin13, pin12, pin11, pin10, pin9
  _74161 u_74161_1 ();  // open: pin1, pin2, pin3, pin4, pin5, pin6, pin7, pin15, pin14, pin13, pin12, pin11, pin10, pin9
endmodule

module RLRegister (
  input  CLOCK,
  input  [7:0] DATA_IN,
  input  LOAD_DIS,
  input  RESET_EN,
  output [7:0] DATA_OUT
);

  wire and_1_out, not_1_out;

  and and_1 (and_1_out, ~LOAD_DIS, CLOCK);  // AND_Gate
  not not_1 (not_1_out, RESET_EN);
  _74273 u_74273_1 (
    .pin1(not_1_out), .pin2(DATA_OUT[0]), .pin3(DATA_IN[0]), .pin4(DATA_IN[1]), .pin5(DATA_OUT[1]),
    .pin6(DATA_OUT[2]), .pin7(DATA_IN[2]), .pin8(DATA_IN[3]), .pin9(DATA_OUT[3]), .pin19(DATA_OUT[7]),
    .pin18(DATA_IN[7]), .pin17(DATA_IN[6]), .pin16(DATA_OUT[6]), .pin15(DATA_OUT[5]), .pin14(DATA_IN[5]),
    .pin13(DATA_IN[4]), .pin12(DATA_OUT[4]), .pin11(and_1_out));
endmodule

module RRegister (
  input  LOAD_CLOCK,
  input  [7:0] DATA_IN,
  input  RESET_DIS,
  output [7:0] DATA_OUT
);

  _74273 u_74273_1 (
    .pin1(RESET_DIS), .pin2(DATA_OUT[0]), .pin3(DATA_IN[0]), .pin4(DATA_IN[1]), .pin5(DATA_OUT[1]),
    .pin6(DATA_OUT[2]), .pin7(DATA_IN[2]), .pin8(DATA_IN[3]), .pin9(DATA_OUT[3]), .pin19(DATA_OUT[7]),
    .pin18(DATA_IN[7]), .pin17(DATA_IN[6]), .pin16(DATA_OUT[6]), .pin15(DATA_OUT[5]), .pin14(DATA_IN[5]),
    .pin13(DATA_IN[4]), .pin12(DATA_OUT[4]), .pin11(LOAD_CLOCK));
endmodule

module RegisterSelector (
  input  A,
  input  B,
  input  C,
  input  EN_OUT_1,
  input  DIS_OUT_2,
  input  DIS_OUT_3,
  output OUT_0,
  output OUT_1,
  output OUT_2,
  output OUT_3,
  output OUT_4,
  output OUT_5,
  output OUT_6,
  output OUT_7
);

  wire and_1_out;
  wire [7:0] decoder_1_out0;

  and and_1 (and_1_out, EN_OUT_1, ~DIS_OUT_2, ~DIS_OUT_3);  // AND_Gate
  Decoder #(.select(3)) decoder_1 (
    .out0(decoder_1_out0[0]), .out1(decoder_1_out0[1]), .out2(decoder_1_out0[2]), .out3(decoder_1_out0[3]),
    .out4(decoder_1_out0[4]), .out5(decoder_1_out0[5]), .out6(decoder_1_out0[6]), .out7(decoder_1_out0[7]),
    .sel({C, B, A}), .en(and_1_out));
  assign {OUT_7, OUT_6, OUT_5, OUT_4, OUT_3, OUT_2, OUT_1, OUT_0} = ~decoder_1_out0;  // NOT_Gate not_1, 8 bits wide
endmodule

module MicrocodeROM (
  input  [7:0] OPCODE,
  input  [3:0] MICRO_COUNT,
  output [7:0] DATA
);

  ROM #(.addrWidth(11)) rom_1 (.addr({OPCODE[6:0], MICRO_COUNT}), .data(DATA));

  // Notes on the sheet:
  //   contents of rom_1 (hex, n*v repeats v):
  //   16*0 2 15*ff 2 15*ff 2 15*ff 2 15*ff 29 29 1966*ff
endmodule
