# Fritzing sketch 8BitProgramCounter (saved by Fritzing 0.9.10b)
breadboards: 1

parts:
  74LS5 = 74LS161 [chip_label=74LS161 package="DIP (Dual Inline) [THT]"]
  74LS6 = 74LS161 [chip_label=74LS161 package="DIP (Dual Inline) [THT]"]
  R1 = Resistor [tolerance=±5% power=0.25 resistance=220 package=THT]
  R2 = Resistor [tolerance=±5% power=0.25 resistance=220 package=THT]
  R3 = Resistor [tolerance=±5% power=0.25 resistance=220 package=THT]
  R4 = Resistor [tolerance=±5% power=0.25 resistance=220 package=THT]
  R9 = Resistor [tolerance=±5% power=0.25 resistance=220 package=THT]
  R10 = Resistor [tolerance=±5% power=0.25 resistance=220 package=THT]
  R11 = Resistor [tolerance=±5% power=0.25 resistance=220 package=THT]
  R12 = Resistor [tolerance=±5% power=0.25 resistance=220 package=THT]

nets:
  N1: 74LS5.-CLR, 74LS6.-CLR, 74LS6.ENP, 74LS6.ENT
  N2: 74LS5.CLK, 74LS6.CLK
  N3: 74LS5.ENP, 74LS5.ENT, 74LS6.RCO
  GND: 74LS5.GND, 74LS6.GND
  VCC: 74LS5.-LOAD, 74LS5.VCC, 74LS6.-LOAD, 74LS6.VCC
  N4: 74LS5.Out_4, R9.Pin_1
  N5: 74LS5.Out_3, R12.Pin_1
  N6: 74LS5.Out_2, R10.Pin_1
  N7: 74LS5.Out_1, R11.Pin_1
  N8: 74LS6.Out_4, R1.Pin_1
  N9: 74LS6.Out_3, R4.Pin_1
  N10: 74LS6.Out_2, R3.Pin_1
  N11: 74LS6.Out_1, R2.Pin_1

custom parts:
  74LS161: 74LS161 synchronous counter with asynchronous clear
