# Fritzing sketch DualModeClock (saved by Fritzing 0.9.10b)
breadboards: 1

parts:
  U2 = 556 [package=dil14]
  R5 = TRIMPOT [maximum_resistance=10kΩ knob_status=50% power=0.5W package=trimpot_pth_s3_lock]
  S2 = Pushbutton [package="[THT]"]
  C3 = Ceramic Capacitor [capacitance=100nF voltage=35V package="100 mil [THT, multilayer]"]
  R6 = Resistor [tolerance=±5% power=0.25 resistance=1M package=THT]
  R7 = Resistor [tolerance=±5% power=0.5W resistance=1M package=THT]
  C4 = Electrolytic Capacitor [capacitance=1µF voltage=35V package="100 mil [THT, electrolytic]"]
  R8 = Resistor [tolerance=±5% power=0.25 resistance=1k package=THT]
  R9 = Resistor [tolerance=±5% power=0.5W resistance=1k package=THT]
  C5 = Ceramic Capacitor [capacitance=100nF voltage=35V package="100 mil [THT, multilayer]"]
  C6 = Electrolytic Capacitor [capacitance=1µF voltage=35V package="100 mil [THT, electrolytic]"]
  S3 = Toggle Switch [package=THT]
  U3 = 4001 4 x 2 Input NOR Gate, single part [part_number=4001 package="DIP (Dual Inline) [THT]"]
  U4 = 4001 4 x 2 Input NOR Gate, single part [part_number=4001 package="DIP (Dual Inline) [THT]"]
  R10 = Resistor [tolerance=±5% power=0.25 resistance=1k package=THT]
  LED1 = smd LED [color="Red (633nm)" package="1206 [SMD]"]

nets:
  N1: U2.DIS, U2.THR, R7.Pin_1, C4.+
  N2: U2.CV, C3.1
  VDD: U2.RST, U2.RST2, U2.VCC, R6.Pin_0, R7.Pin_0, R9.Pin_1, S3.COM, U3.VDD, U4.VDD
  N3: U2.OUT, U4.Q1
  N4: U2.TRIG, S2.Pin_3, S2.Pin_4, R6.Pin_1
  GND: U2.GND, S2.Pin_1, S2.Pin_2, C3.0, C4.-, C5.0, C6.-, U3.GND, U4.GND, U4.A3, LED1.cathode
  N5: U2.TRIG2, U2.THR2, R5.WIPER, C6.+
  N6: U2.OUT2, U3.A4
  N7: U2.CV2, C5.1
  N8: U2.DIS2, R8.Pin_0, R9.Pin_0
  N9: R5.CW, R8.Pin_1
  N10: S3.L1, U3.Q1
  N11: S3.L2, U3.A2
  N12: U3.A1, U3.B2, U4.B1
  N13: U3.B1, U3.Q2, U3.Q4
  N14: U3.A3, U4.A1
  N15: U3.B3, U3.B4
  N16: U3.Q3, U4.Q4, U4.A4
  N17: U4.B3, U4.B4
  N18: U4.Q3, R10.Pin_0
  N19: R10.Pin_1, LED1.anode
