# Fritzing sketch ProgramROMWithTristate (saved by Fritzing 0.9.10b)
breadboards: 2

parts:
  U1 = ZIFSOCKET-40-6 [package=dil40-6-zif_socket]
  U2 = ZIFSOCKET-40-6 [package=dil40-6-zif_socket]
  IC1 = DIP - 20 pins [chip_label=74LS245 package="DIP (Dual Inline) [THT]"]

nets:
  N1: U1.P$1, U1.P$2, U1.P$14, U2.P$32, U2.P$33, U2.P$34, U2.P$35, U2.P$36, U2.P$37, U2.P$38
  N2: U1.P$3, U2.P$3
  N3: U1.P$4, U2.P$4
  N4: U1.P$5, U2.P$5
  N5: U1.P$6, U2.P$6
  N6: U1.P$7, U2.P$7
  N7: U1.P$8, U2.P$8
  N8: U1.P$9, U2.P$9
  N9: U1.P$32, U1.P$33, U1.P$34, U1.P$35, U1.P$36, U1.P$37, U1.P$38, U2.P$1, U2.P$2, U2.P$14, IC1.DIR, IC1.GND
  N10: U1.P$39, U1.P$40, U2.P$10, U2.P$39
  N11: U2.P$11, IC1.B1
  N12: U2.P$12, IC1.B2
  N13: U2.P$13, IC1.B3
  N14: U2.P$27, IC1.B4
  N15: U2.P$28, IC1.B5
  N16: U2.P$29, IC1.B6
  N17: U2.P$30, IC1.B7
  N18: U2.P$31, IC1.B8

custom parts:
  DIP - 20 pins: A DIP stand-in part for whatever IC you want. With 20 pins on a 300mil dual inline package (DIP) footprint.
