// Logisim project 8BitComp.circ as structural Verilog: 15 circuits, main circuit main
module RegisterThing (
  input  [7:0] BUS_IN,
  input  CLOCK,
  input  LOAD_EN,
  input  BUS_OUT_EN,
  output [7:0] BUS_OUT,
  output [7:0] DATA
);

  Register register_1 (.D(BUS_IN), .en(LOAD_EN), .clk(CLOCK), .Q(DATA));  // open: clr
  assign BUS_OUT = BUS_OUT_EN ? DATA : 8'bz;  // Controlled_Buffer controlled_buffer_1
endmodule

module main (
  input  HALT,
  input  in_2,
  input  CLOCK_MODE,
  input  CLOCK_BUTTON,
  input  [3:0] PROG_SELECT,
  input  in_6,
  input  in_7,
  input  in_8,
  input  in_9,
  input  in_10,
  input  in_11,
  input  in_12,
  input  in_13
);

  wire ALU_INPUT_MOD, ALU_INVERT_OUT, ALU_REPLACE_B, and_1_out, clock_1_out, clock_2_out, clock_3_out,
       clock_4_out, clock_5_out, clock_6_out, clock_8_out, clock_9_out, comparator_1_eq, comparator_1_gt,
       DATA_OUT_DIS, decoder_2_out0, decoder_2_out1, GAMEPAD_LATCH, INST_NOT_DONE, JUMP_DIS,
       MASTER_RESET_DIS, nALU_B_SEL_SYS, nand_3_out, nand_4_out, nand_5_out, nand_6_out, nand_7_out, nCLOCK,
       nDISPLAY_INIT, nDISPLAY_SHOW, nGAMEPAD_LATCH, nJUMP_COND, nJUMP_INST, nor_1_out, nor_2_out, nor_3_out,
       nor_4_out, nor_5_out, nor_6_out, nor_7_out, nor_8_out, nor_9_out, nor_10_out, nor_11_out, not_4_out,
       not_6_out, not_7_out, not_8_out, not_10_out, not_11_out, not_12_out, not_13_out, not_14_out,
       not_15_out, not_16_out, not_17_out, not_18_out, not_19_out, not_20_out, not_21_out, not_22_out,
       not_23_out, not_24_out, not_25_out, not_26_out, not_27_out, or_1_out, PC_OUT_DIS,
       pisoshiftregister_1_serial_out, RAM_ADDR_FROM_DATA, RAM_IN_DIS, RAM_OUT_DIS, RAM_RW, REG_IN_DIS,
       REG_OUT_DIS, RegisterLoadSelector_out_0, RegisterLoadSelector_out_1, RegisterLoadSelector_out_2,
       RegisterLoadSelector_out_3, RegisterLoadSelector_out_4, registerselector_1_out_0,
       registerselector_1_out_1, registerselector_1_out_2, registerselector_1_out_3,
       registerselector_1_out_4, registerselector_2_out_0, registerselector_2_out_1,
       registerselector_2_out_2, registerselector_2_out_3, USER_INPUT_DIS;
  wire [1:0] ALU_B_SEL, ALU_SELECT;
  wire [2:0] IO_ROM_data, IO_ROM_data_2, REG_OUT_SEL, SET_REG_SEL;
  wire [3:0] microcodecounter_1_address;
  wire [5:0] not_2_out;
  wire [6:0] ALUOutRegister_data_out;
  wire [7:0] adder_1_out, ADDR_REG, bit_extender_1_out, bit_extender_2_out, bit_extender_3_out,
       bit_extender_4_out, bit_extender_5_out, bit_extender_6_out, controlled_buffer_5_out, DATA_ROM_data,
       decoder_1_out0, decoder_3_out0, multiplexer_3_out, multiplexer_4_out, multiplexer_5_out,
       multiplexer_6_out, nand_8_out, not_5_out, OPCODE_ROM_data, programcounter_1_address, ram_1_data,
       RealPC_data_out, Reg0_data_out, Reg1_data_out, Reg2_data_out, Reg3_data_out,
       siposhiftregister_1_parallel_out, xor_1_out, xor_2_out, xor_3_out, xor_4_out, xor_5_out;
  wire [63:0] displaydecoder_1_display_out;

  not not_1 (MASTER_RESET_DIS, in_2);
  ROM #(.addrWidth(12)) OPCODE_ROM (
    .addr({PROG_SELECT[2], PROG_SELECT[3], PROG_SELECT[1:0], RealPC_data_out}), .data(OPCODE_ROM_data));
  Clock clock_1 (.out(clock_1_out));
  Decoder #(.select(3)) decoder_1 (
    .out0(decoder_1_out0[0]), .out1(decoder_1_out0[1]), .out2(decoder_1_out0[2]), .out3(decoder_1_out0[3]),
    .out4(decoder_1_out0[4]), .out5(decoder_1_out0[5]), .out6(decoder_1_out0[6]), .out7(decoder_1_out0[7]),
    .sel(IO_ROM_data_2), .en(REG_IN_DIS));
  nand nand_1 (RAM_RW, clock_1_out, not_7_out);
  nand nand_2 (JUMP_DIS, not_4_out, not_8_out);
  assign {nDISPLAY_SHOW, nDISPLAY_INIT, not_2_out[5], nGAMEPAD_LATCH, RAM_IN_DIS, nJUMP_INST, not_2_out[1:0]} = ~decoder_1_out0;  // NOT_Gate not_2, 8 bits wide
  Clock clock_2 (.out(clock_2_out));
  Decoder #(.enable("false")) decoder_2 (.out0(decoder_2_out0), .out1(decoder_2_out1), .sel(CLOCK_MODE));
  LedBar IO_FLAGS (
    .led0(REG_IN_DIS), .led1(IO_ROM_data_2[2]), .led2(IO_ROM_data_2[1]), .led3(IO_ROM_data_2[0]),
    .led4(REG_OUT_DIS), .led5(IO_ROM_data[2]), .led6(IO_ROM_data[1]), .led7(IO_ROM_data[0]));
  nor nor_1 (nor_1_out, clock_2_out, nor_4_out);
  nor nor_2 (nor_2_out, nor_6_out, nor_1_out);
  nor nor_3 (nor_3_out, nor_4_out, decoder_2_out1);
  nor nor_4 (nor_4_out, nor_3_out, decoder_2_out0);
  LedBar #(.matrixcols(4)) ledbar_1 (
    .led0(microcodecounter_1_address[3]), .led1(microcodecounter_1_address[2]),
    .led2(microcodecounter_1_address[1]), .led3(microcodecounter_1_address[0]));
  Clock clock_3 (.out(clock_3_out));
  Decoder #(.select(3)) decoder_3 (
    .out0(decoder_3_out0[0]), .out1(decoder_3_out0[1]), .out2(decoder_3_out0[2]), .out3(decoder_3_out0[3]),
    .out4(decoder_3_out0[4]), .out5(decoder_3_out0[5]), .out6(decoder_3_out0[6]), .out7(decoder_3_out0[7]),
    .sel(IO_ROM_data), .en(REG_OUT_DIS));
  nand nand_3 (nand_3_out, nDISPLAY_SHOW, nDISPLAY_INIT);
  nand nand_4 (nand_4_out, nDISPLAY_INIT, nDISPLAY_INIT);
  nor nor_5 (nor_5_out, nor_2_out, nor_2_out);
  nor nor_6 (nor_6_out, nor_3_out, CLOCK_BUTTON);
  ROM #(.addrWidth(11)) IO_ROM (
    .addr({OPCODE_ROM_data[6:0], microcodecounter_1_address}),
    .data({REG_IN_DIS, IO_ROM_data_2, REG_OUT_DIS, IO_ROM_data}));
  MicrocodeCounter microcodecounter_1 (
    .CLOCK(nCLOCK), .SYNC_RESET_DIS(INST_NOT_DONE), .ASYNC_RESET_DIS(MASTER_RESET_DIS),
    .COUNT_EN(INST_NOT_DONE), .ADDRESS(microcodecounter_1_address));
  not not_3 (nCLOCK, clock_3_out);
  not not_4 (not_4_out, nJUMP_INST);
  assign {not_5_out[7:5], USER_INPUT_DIS, RAM_OUT_DIS, PC_OUT_DIS, DATA_OUT_DIS, not_5_out[0]} = ~decoder_3_out0;  // NOT_Gate not_5, 8 bits wide
  Clock clock_4 (.out(clock_4_out));
  nor nor_7 (nor_7_out, nor_5_out, HALT);
  LedBar OPCODE (
    .led0(OPCODE_ROM_data[7]), .led1(OPCODE_ROM_data[6]), .led2(OPCODE_ROM_data[5]),
    .led3(OPCODE_ROM_data[4]), .led4(OPCODE_ROM_data[3]), .led5(OPCODE_ROM_data[2]),
    .led6(OPCODE_ROM_data[1]), .led7(OPCODE_ROM_data[0]));
  not not_6 (not_6_out, INST_NOT_DONE);
  not not_7 (not_7_out, RAM_IN_DIS);
  nand nand_5 (nand_5_out, nand_3_out, clock_4_out);
  nand nand_6 (nand_6_out, IO_ROM_data_2[2], IO_ROM_data_2[1]);
  ROM #(.addrWidth(11)) ALU_ROM (
    .addr({OPCODE_ROM_data[6:0], microcodecounter_1_address}),
    .data({INST_NOT_DONE, RAM_ADDR_FROM_DATA, nALU_B_SEL_SYS, ALU_INPUT_MOD, ALU_INVERT_OUT, ALU_REPLACE_B, ALU_SELECT}));
  not not_8 (not_8_out, nJUMP_COND);
  not not_9 (GAMEPAD_LATCH, nGAMEPAD_LATCH);
  LedBar #(.matrixcols(3)) ledbar_2 (.led0(SET_REG_SEL[2]), .led1(SET_REG_SEL[1]), .led2(SET_REG_SEL[0]));
  Multiplexer #(.width(3)) multiplexer_1 (
    .in0(DATA_ROM_data[7:5]), .in1(IO_ROM_data_2), .out(SET_REG_SEL), .sel(nand_6_out));
  SIPOShiftRegister siposhiftregister_1 (
    .OUTPUT_DIS(nDISPLAY_SHOW), .RESET_DIS(MASTER_RESET_DIS), .SR_CLOCK(nand_5_out), .R_CLOCK(nand_5_out),
    .SERIAL_IN(nand_4_out), .PARALLEL_OUT(siposhiftregister_1_parallel_out));  // open: SERIAL_OUT
  Clock clock_5 (.out(clock_5_out));
  LedBar ACTIVE_PC (
    .led0(RealPC_data_out[7]), .led1(RealPC_data_out[6]), .led2(RealPC_data_out[5]),
    .led3(RealPC_data_out[4]), .led4(RealPC_data_out[3]), .led5(RealPC_data_out[2]),
    .led6(RealPC_data_out[1]), .led7(RealPC_data_out[0]));
  RRegister RealPC (
    .LOAD_CLOCK(nCLOCK), .DATA_IN(programcounter_1_address), .RESET_DIS(MASTER_RESET_DIS),
    .DATA_OUT(RealPC_data_out));
  ROM #(.addrWidth(12)) DATA_ROM (
    .addr({PROG_SELECT[2], PROG_SELECT[3], PROG_SELECT[1:0], RealPC_data_out}),
    .data({DATA_ROM_data[7:5], ALU_B_SEL, DATA_ROM_data[2:0]}));
  LedBar #(.matrixcols(3)) ledbar_3 (.led0(REG_OUT_SEL[2]), .led1(REG_OUT_SEL[1]), .led2(REG_OUT_SEL[0]));
  Multiplexer #(.width(3)) multiplexer_2 (
    .in0(DATA_ROM_data[2:0]), .in1(IO_ROM_data), .out(REG_OUT_SEL), .sel(nand_7_out));
  nand nand_7 (nand_7_out, IO_ROM_data[2], IO_ROM_data[1]);
  LedBar ledbar_4 (
    .led0(siposhiftregister_1_parallel_out[7]), .led1(siposhiftregister_1_parallel_out[6]),
    .led2(siposhiftregister_1_parallel_out[5]), .led3(siposhiftregister_1_parallel_out[4]),
    .led4(siposhiftregister_1_parallel_out[3]), .led5(siposhiftregister_1_parallel_out[2]),
    .led6(siposhiftregister_1_parallel_out[1]), .led7(siposhiftregister_1_parallel_out[0]));
  Clock clock_6 (.out(clock_6_out));
  or or_1 (or_1_out, nand_4_out, not_10_out);
  not not_10 (not_10_out, MASTER_RESET_DIS);
  ProgramCounter programcounter_1 (
    .BUS_IN(ram_1_data), .CLOCK(clock_5_out), .RESET_DIS(MASTER_RESET_DIS), .LOAD_DIS(JUMP_DIS),
    .COUNT_EN(not_6_out), .ADDRESS(programcounter_1_address));
  LedBar PC (
    .led0(programcounter_1_address[7]), .led1(programcounter_1_address[6]),
    .led2(programcounter_1_address[5]), .led3(programcounter_1_address[4]),
    .led4(programcounter_1_address[3]), .led5(programcounter_1_address[2]),
    .led6(programcounter_1_address[1]), .led7(programcounter_1_address[0]));
  RAM #(.clearpin("true"), .databus("bidir"), .enables("line"), .trigger("high")) ram_1 (
    .addr(multiplexer_3_out), .we(not_11_out), .oe(and_1_out), .clk(MASTER_RESET_DIS), .data(ram_1_data),
    .clr(not_12_out));
  not not_11 (not_11_out, RAM_RW);
  and and_1 (and_1_out, MASTER_RESET_DIS, ~RAM_OUT_DIS);  // AND_Gate
  not not_12 (not_12_out, MASTER_RESET_DIS);
  DisplayDecoder displaydecoder_1 (
    .ROWS(ram_1_data), .COLUMN(siposhiftregister_1_parallel_out), .CLOCK(clock_6_out),
    .RESET_ASYNC(or_1_out), .DISPLAY_OUT(displaydecoder_1_display_out));
  LedBar DATA (
    .led0(DATA_ROM_data[7]), .led1(DATA_ROM_data[6]), .led2(DATA_ROM_data[5]), .led3(ALU_B_SEL[1]),
    .led4(ALU_B_SEL[0]), .led5(DATA_ROM_data[2]), .led6(DATA_ROM_data[1]), .led7(DATA_ROM_data[0]));
  DotMatrix #(.inputtype("row"), .matrixcols(8), .matrixrows(8)) dotmatrix_1 (
    .row0(displaydecoder_1_display_out[7:0]), .row1(displaydecoder_1_display_out[15:8]),
    .row2(displaydecoder_1_display_out[23:16]), .row3(displaydecoder_1_display_out[31:24]),
    .row4(displaydecoder_1_display_out[39:32]), .row5(displaydecoder_1_display_out[47:40]),
    .row6(displaydecoder_1_display_out[55:48]), .row7(displaydecoder_1_display_out[63:56]));
  assign ram_1_data = not_13_out ? programcounter_1_address : 8'bz;  // Controlled_Buffer controlled_buffer_1
  not not_13 (not_13_out, PC_OUT_DIS);
  not not_14 (not_14_out, DATA_OUT_DIS);
  LedBar ledbar_5 (
    .led0(multiplexer_3_out[7]), .led1(multiplexer_3_out[6]), .led2(multiplexer_3_out[5]),
    .led3(multiplexer_3_out[4]), .led4(multiplexer_3_out[3]), .led5(multiplexer_3_out[2]),
    .led6(multiplexer_3_out[1]), .led7(multiplexer_3_out[0]));
  Multiplexer #(.width(8)) multiplexer_3 (
    .in0(ADDR_REG), .in1({DATA_ROM_data[7:5], ALU_B_SEL, DATA_ROM_data[2:0]}), .out(multiplexer_3_out),
    .sel(RAM_ADDR_FROM_DATA));
  assign ram_1_data = not_14_out ? {DATA_ROM_data[7:5], ALU_B_SEL, DATA_ROM_data[2:0]} : 8'bz;  // Controlled_Buffer controlled_buffer_2
  LedBar ledbar_6 (
    .led0(ram_1_data[7]), .led1(ram_1_data[6]), .led2(ram_1_data[5]), .led3(ram_1_data[4]),
    .led4(ram_1_data[3]), .led5(ram_1_data[2]), .led6(ram_1_data[1]), .led7(ram_1_data[0]));
  LedBar ledbar_7 (
    .led0(ram_1_data[7]), .led1(ram_1_data[6]), .led2(ram_1_data[5]), .led3(ram_1_data[4]),
    .led4(ram_1_data[3]), .led5(ram_1_data[2]), .led6(ram_1_data[1]), .led7(ram_1_data[0]));
  Pull_Resistor pull_resistor_1 (.node(ram_1_data[7]));
  Pull_Resistor pull_resistor_2 (.node(ram_1_data[6]));
  Pull_Resistor pull_resistor_3 (.node(ram_1_data[5]));
  Pull_Resistor pull_resistor_4 (.node(ram_1_data[4]));
  Pull_Resistor pull_resistor_5 (.node(ram_1_data[3]));
  Pull_Resistor pull_resistor_6 (.node(ram_1_data[2]));
  Pull_Resistor pull_resistor_7 (.node(ram_1_data[1]));
  Pull_Resistor pull_resistor_8 (.node(ram_1_data[0]));
  not not_15 (not_15_out, USER_INPUT_DIS);
  assign ram_1_data[7] = not_15_out ? pisoshiftregister_1_serial_out : 1'bz;  // Controlled_Buffer controlled_buffer_3
  RRegister Reg0 (
    .LOAD_CLOCK(RegisterLoadSelector_out_0), .DATA_IN({nJUMP_COND, ALUOutRegister_data_out}),
    .RESET_DIS(MASTER_RESET_DIS), .DATA_OUT(Reg0_data_out));
  not not_16 (not_16_out, registerselector_1_out_0);
  assign ram_1_data = not_16_out ? Reg0_data_out : 8'bz;  // Controlled_Buffer controlled_buffer_4
  LedBar ledbar_8 (
    .led0(Reg0_data_out[7]), .led1(Reg0_data_out[6]), .led2(Reg0_data_out[5]), .led3(Reg0_data_out[4]),
    .led4(Reg0_data_out[3]), .led5(Reg0_data_out[2]), .led6(Reg0_data_out[1]), .led7(Reg0_data_out[0]));
  not not_17 (not_17_out, registerselector_2_out_0);
  assign controlled_buffer_5_out = not_17_out ? Reg0_data_out : 8'bz;  // Controlled_Buffer controlled_buffer_5
  LedBar ledbar_9 (
    .led0(controlled_buffer_5_out[7]), .led1(controlled_buffer_5_out[6]), .led2(controlled_buffer_5_out[5]),
    .led3(controlled_buffer_5_out[4]), .led4(controlled_buffer_5_out[3]), .led5(controlled_buffer_5_out[2]),
    .led6(controlled_buffer_5_out[1]), .led7(controlled_buffer_5_out[0]));
  nor nor_8 (nor_8_out, ALU_INPUT_MOD, ALU_INPUT_MOD);
  Multiplexer #(.width(8)) multiplexer_4 (
    .in0(controlled_buffer_5_out), .in1({8{1'b1}}), .out(multiplexer_4_out), .sel(ALU_REPLACE_B));
  nor nor_9 (nor_9_out, ALU_INVERT_OUT, ALU_INVERT_OUT);
  Clock clock_7 ();  // open: out
  assign bit_extender_1_out = {{7{nor_10_out}}, nor_10_out};  // Bit_Extender bit_extender_1
  nor nor_10 (nor_10_out, nor_8_out, ALU_REPLACE_B);
  assign bit_extender_2_out = {{7{ALU_INPUT_MOD}}, ALU_INPUT_MOD};  // Bit_Extender bit_extender_2
  assign bit_extender_3_out = {{7{nor_11_out}}, nor_11_out};  // Bit_Extender bit_extender_3
  nor nor_11 (nor_11_out, nor_9_out, ALU_INPUT_MOD);
  assign xor_1_out = ram_1_data ^ bit_extender_1_out;  // XOR_Gate xor_1, 8 bits wide
  assign xor_2_out = multiplexer_4_out ^ bit_extender_2_out;  // XOR_Gate xor_2, 8 bits wide
  assign xor_3_out = ram_1_data ^ bit_extender_3_out;  // XOR_Gate xor_3, 8 bits wide
  PISOShiftRegister pisoshiftregister_1 (
    .PARALLEL_IN({in_6, in_7, in_8, in_9, in_10, in_11, in_12, in_13}), .LATCH(GAMEPAD_LATCH),
    .CLOCK(nCLOCK), .SERIAL_OUT(pisoshiftregister_1_serial_out));
  RRegister Reg1 (
    .LOAD_CLOCK(RegisterLoadSelector_out_1), .DATA_IN({nJUMP_COND, ALUOutRegister_data_out}),
    .RESET_DIS(MASTER_RESET_DIS), .DATA_OUT(Reg1_data_out));
  not not_18 (not_18_out, registerselector_1_out_1);
  assign ram_1_data = not_18_out ? Reg1_data_out : 8'bz;  // Controlled_Buffer controlled_buffer_6
  LedBar ledbar_10 (
    .led0(Reg1_data_out[7]), .led1(Reg1_data_out[6]), .led2(Reg1_data_out[5]), .led3(Reg1_data_out[4]),
    .led4(Reg1_data_out[3]), .led5(Reg1_data_out[2]), .led6(Reg1_data_out[1]), .led7(Reg1_data_out[0]));
  not not_19 (not_19_out, registerselector_2_out_1);
  assign controlled_buffer_5_out = not_19_out ? Reg1_data_out : 8'bz;  // Controlled_Buffer controlled_buffer_7
  not not_20 (not_20_out, comparator_1_gt);
  not not_21 (not_21_out, comparator_1_eq);
  Comparator #(.mode("unsigned")) comparator_1 (
    .a(xor_1_out), .b(xor_2_out), .gt(comparator_1_gt), .eq(comparator_1_eq));  // open: lt
  assign bit_extender_4_out = {{7{not_20_out}}, not_20_out};  // Bit_Extender bit_extender_4
  assign bit_extender_5_out = {{7{not_21_out}}, not_21_out};  // Bit_Extender bit_extender_5
  Adder adder_1 (.a(xor_3_out), .b(xor_2_out), .out(adder_1_out));  // open: cin, cout
  assign xor_4_out = ram_1_data ^ controlled_buffer_5_out;  // XOR_Gate xor_4, 8 bits wide
  Multiplexer #(.width(8)) multiplexer_5 (
    .in0(xor_4_out), .in1({1'b0, ram_1_data[7:1]}), .out(multiplexer_5_out), .sel(ALU_INPUT_MOD));
  LedBar ledbar_11 (
    .led0(adder_1_out[7]), .led1(adder_1_out[6]), .led2(adder_1_out[5]), .led3(adder_1_out[4]),
    .led4(adder_1_out[3]), .led5(adder_1_out[2]), .led6(adder_1_out[1]), .led7(adder_1_out[0]));
  RRegister Reg2 (
    .LOAD_CLOCK(RegisterLoadSelector_out_2), .DATA_IN({nJUMP_COND, ALUOutRegister_data_out}),
    .RESET_DIS(MASTER_RESET_DIS), .DATA_OUT(Reg2_data_out));
  not not_22 (not_22_out, registerselector_1_out_2);
  assign ram_1_data = not_22_out ? Reg2_data_out : 8'bz;  // Controlled_Buffer controlled_buffer_8
  LedBar ledbar_12 (
    .led0(Reg2_data_out[7]), .led1(Reg2_data_out[6]), .led2(Reg2_data_out[5]), .led3(Reg2_data_out[4]),
    .led4(Reg2_data_out[3]), .led5(Reg2_data_out[2]), .led6(Reg2_data_out[1]), .led7(Reg2_data_out[0]));
  not not_23 (not_23_out, registerselector_2_out_2);
  assign controlled_buffer_5_out = not_23_out ? Reg2_data_out : 8'bz;  // Controlled_Buffer controlled_buffer_9
  assign nand_8_out = ~(xor_1_out & xor_2_out);  // NAND_Gate nand_8, 8 bits wide
  Multiplexer #(.select(3), .width(8)) multiplexer_6 (
    .in0(adder_1_out), .in1(bit_extender_4_out), .in2(bit_extender_5_out), .in3(nand_8_out),
    .in4(bit_extender_5_out), .in5(bit_extender_4_out), .in6(adder_1_out), .in7(multiplexer_5_out),
    .out(multiplexer_6_out), .sel({ALU_REPLACE_B, ALU_SELECT}));
  RRegister Reg3 (
    .LOAD_CLOCK(RegisterLoadSelector_out_3), .DATA_IN({nJUMP_COND, ALUOutRegister_data_out}),
    .RESET_DIS(MASTER_RESET_DIS), .DATA_OUT(Reg3_data_out));
  not not_24 (not_24_out, registerselector_1_out_3);
  assign ram_1_data = not_24_out ? Reg3_data_out : 8'bz;  // Controlled_Buffer controlled_buffer_10
  not not_25 (not_25_out, registerselector_2_out_3);
  assign controlled_buffer_5_out = not_25_out ? Reg3_data_out : 8'bz;  // Controlled_Buffer controlled_buffer_11
  LedBar ledbar_13 (
    .led0(Reg3_data_out[7]), .led1(Reg3_data_out[6]), .led2(Reg3_data_out[5]), .led3(Reg3_data_out[4]),
    .led4(Reg3_data_out[3]), .led5(Reg3_data_out[2]), .led6(Reg3_data_out[1]), .led7(Reg3_data_out[0]));
  assign bit_extender_6_out = {{7{ALU_INVERT_OUT}}, ALU_INVERT_OUT};  // Bit_Extender bit_extender_6
  RRegister Reg4 (
    .LOAD_CLOCK(RegisterLoadSelector_out_4), .DATA_IN({nJUMP_COND, ALUOutRegister_data_out}),
    .RESET_DIS(MASTER_RESET_DIS), .DATA_OUT(ADDR_REG));
  not not_26 (not_26_out, registerselector_1_out_4);
  assign ram_1_data = not_26_out ? ADDR_REG : 8'bz;  // Controlled_Buffer controlled_buffer_12
  not not_27 (not_27_out, nALU_B_SEL_SYS);
  assign controlled_buffer_5_out = not_27_out ? ADDR_REG : 8'bz;  // Controlled_Buffer controlled_buffer_13
  LedBar ledbar_14 (
    .led0(xor_5_out[7]), .led1(xor_5_out[6]), .led2(xor_5_out[5]), .led3(xor_5_out[4]), .led4(xor_5_out[3]),
    .led5(xor_5_out[2]), .led6(xor_5_out[1]), .led7(xor_5_out[0]));
  assign xor_5_out = bit_extender_6_out ^ multiplexer_6_out;  // XOR_Gate xor_5, 8 bits wide
  LedBar ledbar_15 (
    .led0(ADDR_REG[7]), .led1(ADDR_REG[6]), .led2(ADDR_REG[5]), .led3(ADDR_REG[4]), .led4(ADDR_REG[3]),
    .led5(ADDR_REG[2]), .led6(ADDR_REG[1]), .led7(ADDR_REG[0]));
  Clock clock_8 (.out(clock_8_out));
  Clock clock_9 (.out(clock_9_out));
  RegisterSelector RegisterLoadSelector (
    .A(SET_REG_SEL[0]), .B(SET_REG_SEL[1]), .C(SET_REG_SEL[2]), .EN_OUT_1(clock_8_out),
    .DIS_OUT_2(REG_IN_DIS), .DIS_OUT_3(1'b0), .OUT_0(RegisterLoadSelector_out_0),
    .OUT_1(RegisterLoadSelector_out_1), .OUT_2(RegisterLoadSelector_out_2),
    .OUT_3(RegisterLoadSelector_out_3), .OUT_4(RegisterLoadSelector_out_4));  // open: OUT_5, OUT_6, OUT_7
  RegisterSelector registerselector_1 (
    .A(REG_OUT_SEL[0]), .B(REG_OUT_SEL[1]), .C(REG_OUT_SEL[2]), .EN_OUT_1(1'b1), .DIS_OUT_2(1'b0),
    .DIS_OUT_3(REG_OUT_DIS), .OUT_0(registerselector_1_out_0), .OUT_1(registerselector_1_out_1),
    .OUT_2(registerselector_1_out_2), .OUT_3(registerselector_1_out_3), .OUT_4(registerselector_1_out_4));  // open: OUT_5, OUT_6, OUT_7
  RegisterSelector registerselector_2 (
    .A(ALU_B_SEL[0]), .B(ALU_B_SEL[1]), .C(1'b0), .EN_OUT_1(nALU_B_SEL_SYS), .DIS_OUT_2(1'b0),
    .DIS_OUT_3(1'b0), .OUT_0(registerselector_2_out_0), .OUT_1(registerselector_2_out_1),
    .OUT_2(registerselector_2_out_2), .OUT_3(registerselector_2_out_3));  // open: OUT_4, OUT_5, OUT_6, OUT_7
  RRegister ALUOutRegister (
    .LOAD_CLOCK(clock_9_out), .DATA_IN(xor_5_out), .RESET_DIS(MASTER_RESET_DIS),
    .DATA_OUT({nJUMP_COND, ALUOutRegister_data_out}));
  LedBar ledbar_16 (
    .led0(nJUMP_COND), .led1(ALUOutRegister_data_out[6]), .led2(ALUOutRegister_data_out[5]),
    .led3(ALUOutRegister_data_out[4]), .led4(ALUOutRegister_data_out[3]), .led5(ALUOutRegister_data_out[2]),
    .led6(ALUOutRegister_data_out[1]), .led7(ALUOutRegister_data_out[0]));

  // Other names for the same wires on the sheet: ALU_SELECT[2] = ALU_REPLACE_B

  // Notes on the sheet:
  //   contents of OPCODE_ROM (hex, n*v repeats v):
  //   254*0 7 1 70 10 70 11 12 12 5 8*30 16*12 5 10*30 5 12*30 5 14 64 7f 31 30 30 3 64 21 29 19 14 40 61
  //   65 50 29 1a 4 60 1 50 61 2a 1a 57 61 25 26 1 64 61 65 21 22 9 2 40 61 21 50 1a 42 61 20 3 64 2 65 31
  //   31 1 2 48 31 3 58 2a 1a 20 61 16 60 16 20 61 59 60 57 58 20 61 12 71 60 12 72 65 122*7f 2 10 2 10 2
  //   10 2 10 2 10 2 10 2 10 2 10 5 4 0 73 74 60 234*7f 2 10 2 10 2 10 2 10 2 10 2 10 2 10 2 10 5 4 0 73
  //   74 74 74 60 1256*7f 2 10 2 10 2 10 2 10 2 10 2 10 2 10 2 10 5 4 0 73 6*74 60 229*7f a 2 6 1b 2 10 64
  //   2 10 64 2 10 64 2 10 2 10 2 10 2 4*10 2 10 2 10 2 10 2 10 6b 8 73 74 60 25 3 4 64 8 1 70 59 63 3 6c
  //   6d 6e 6f 60 8 8 8 14 50 7 4 58 62 11 14 64 6 14 50 58 15 50 58 24 25 16 40 16 40 58 24 61 20 64 24 4
  //   58 25 56 58 24 64 62 20 10 20 10 28 1a 57 58 18 60 21 20 64 62 20 28 1a 57 58 18 20 21 11 10 16 15 6
  //   58 55 25 29 1a 3 60 4*50 7 63 57 58 59 20 28 18 14 7 6 58 10 20 63 64 60 14 15 64 4 2 3 0 7 63 8 1
  //   63 3 64 8 1 63 9 1 63 64 24 64 64 20 63 60 2 73 74 7 63 65 3 4 62 7 4 62 7 3 4 62 3 65 29 1a 3 60 54
  //   7 63 58 65 a 25 64 20 28 1a 59 18 65 14 15 64 15 14 51 62 6 58 55 29 1a 60 55 7 63 6 58 64 6 14 50
  //   58 11 14 50 58 12 14 7 6 58 10 2 65 62 50 62 61 3 5c 65 5*7f a 2 6 1b 2 10 64 2 10 64 2 10 64 2 10 2
  //   10 2 10 2 4*10 2 10 2 10 2 10 2 10 6b 8 73 74 60 25 3 4 64 8 1 70 59 63 3 6c 6d 6e 6f 60 8 8 8 14 50
  //   7 4 58 62 11 14 64 6 14 50 58 15 50 58 24 25 16 40 16 40 58 24 61 20 64 24 4 58 25 56 58 24 64 62 20
  //   10 20 10 28 1a 57 58 18 60 21 20 64 62 20 28 1a 57 58 18 20 21 11 10 16 15 6 58 55 25 29 1a 3 60
  //   4*50 7 63 57 58 59 20 28 18 14 7 6 58 10 20 63 64 60 14 15 64 4 2 3 64 8 1 63 3 0 8 1 63 9 1 63 64
  //   24 64 64 64 20 63 60 73 74 65 3 4 62 7 4 62 7 3 4 62 3 65 29 1a 3 60 54 7 63 58 65 a 25 64 20 28 1a
  //   59 18 65 14 15 64 15 14 51 62 6 58 55 29 1a 60 55 7 63 6 58 64 6 14 50 58 11 14 50 58 12 14 7 6 58
  //   10 2 65 62 50 62 61 3 5c 65 9*7f 64 64 60 0 1276*7f
  //   contents of IO_ROM (hex, n*v repeats v):
  //   16*88 77 15*88 9 15*88 19 15*88 29 15*88 39 15*88 49 15*88 49 0 49 0 12*88 49 11 49 11 12*88 49 22
  //   49 22 12*88 49 33 49 33 92*88 b0 15*88 b1 15*88 b2 15*88 b3 15*88 b 15*88 1b 15*88 2b 15*88 3b 15*88
  //   b7 15*88 b9 15*88 7b 15*88 b7 44 b7 44 b7 44 b7 44 b7 44 b7 44 b7 44 b7 44 64*88 49 43 b 13*88 49 43
  //   1b 13*88 49 43 2b 29*88 49 43 b0 13*88 49 43 b1 13*88 49 43 b2 29*88 49 40 14*88 49 41 14*88 49 42
  //   94*88 43 b9 33 13*88 43 b7 33 237*88 77 15*88 77 15*88 77 31*88 77 15*88 77 15*88 77 31*88 77 15*88
  //   77 15*88 77 15*88 77 79*88 77 15*88 77 47*88 77 15*88 77 77 14*88 77 77 77 13*88 77 15*88 77 15*88
  //   77 15*88 77 15*88 77 15*88 77 15*88 77 47*88 84 a9 14*88 80 a9 14*88 80 a9 14*88 80 a9 14*88 43 3a
  //   b3 34 84 a9 10*88 49 33 43 84 ab 43*88 c8 8c a9 13*88 c8 88 8c a9 12*88 c8 88 88 8c a9 11*88 c8 88
  //   88 88 8c a9 10*88 c8 4*88 8c a9 9*88 c8 5*88 8c a9 8*88 c8 6*88 8c a9 7*88 c8 7*88 8c a9 6*88 7c
  //   15*88 d7 15*88 e7 15*88 49 e8 f8 13*88 fb 44 fb 44 fb 44 fb 44 fb 44 fb 44 fb 44 fb 44 176*88
  //   contents of ALU_ROM (hex, n*v repeats v):
  //   c 15*0 16 15*0 16 15*0 16 15*0 16 15*0 16 15*0 16 15*0 80 80 98 8 12*0 80 80 98 8 12*0 80 80 98 8
  //   12*0 80 80 98 8 92*0 56 15*0 56 15*0 56 15*0 56 15*0 56 15*0 56 15*0 56 15*0 56 15*0 c 15*0 c 15*0
  //   16 15*0 8c 8e 8c 8e 8c 8e 8c 8e 8c 8e 8c 8e 8c 8e 8c e 64*0 96 80 16 13*0 96 80 16 13*0 96 80 16
  //   29*0 96 80 c 13*0 96 80 c 13*0 96 80 c 29*0 96 15*0 96 15*0 96 95*0 96 8c e 13*0 96 8c e 237*0 2a
  //   15*0 1c 15*0 c 31*0 22 15*0 14 15*0 4 31*0 29 15*0 31 15*0 39 15*0 21 79*0 20 15*0 28 47*0 17 15*0
  //   97 17 14*0 97 97 17 13*0 1e 15*0 2b 15*0 33 15*0 3b 15*0 3b 15*0 27 15*0 2f 47*0 87 c 14*0 96 c 14*0
  //   94 c 14*0 9c c 14*0 96 8e 8c 8e 87 c 10*0 96 90 96 87 c 43*0 8c 96 c 13*0 8c 8c 96 c 12*0 8c 8c 8c
  //   96 c 11*0 4*8c 96 c 10*0 5*8c 96 c 9*0 6*8c 96 c 8*0 7*8c 96 c 7*0 8*8c 96 c 6*0 16 15*0 c 15*0 c
  //   15*0 96 8c c 13*0 8c 8e 8c 8e 8c 8e 8c 8e 8c 8e 8c 8e 8c 8e 8c e 160*0 16*8c
  //   contents of DATA_ROM (hex, n*v repeats v):
  //   254*0 1 80 0 80 20 81 82 83 88 1 2 4 8 10 20 40 80 90 91 92 93 94 95 96 97 98 99 9a 9b 9c 9d 9e 9f 0
  //   0 4 0 4 8 10 14 10 8 10 10 0 a 0 5 3 a 0 35 1c 28 0 18 20 80 3b 4*0 ff 69 fd 90 ff 81 1 47 3 29 1 20
  //   f 62 1 29 5b 90 0 0 5b ff fe 2 3b 59 3 ff fe ff 7 10 62 fd 89 20 2 4c fd 0 69 0 3 1 0 40 7 2 0 77 4a
  //   88 20 ff 77 83 78 82 fd 7c 4a 7e 21 4a ff 83 83 2 85 82 2 3 122*0 80 0 c0 1 e0 2 f0 3 f8 4 fc 5 fe 6
  //   ff 7 ff 4*0 11 234*0 80 0 c0 1 e0 2 f0 3 f8 4 fc 5 fe 6 ff 7 ff 6*0 11 1256*0 80 0 c0 1 e0 2 f0 3 f8
  //   4 fc 5 fe 6 ff 7 ff 9*0 11 229*0 7 ff a0 0 bf a3 ad 9f a3 ad 8f a3 ad 0 85 fd a5 f 90 3 8f 80 81 83
  //   2 84 1 82 6 b0 5 b1 25 1 a0 0 20 fc 3 0 ad ff 1 80 54 28 0 37 36 35 34 3e 1 1 1 8f 1 ff 3 2 3e 8f 8f
  //   b3 7 80 21 c 81 4a 34 ff fe b0 2 b1 2a 8 f9 65 fc f4 fc 7 22 fa 0 2 fb bf 50 fb b0 fa b1 a0 40 21 51
  //   2 6f fe ff bf 92 fe a0 40 21 51 2 fe ff 80 81 8f 84 3 c 21 fd 90 80 3 82 52 52 29 29 ff 7d 21 8c 34
  //   fd 90 1 84 1 3f 4 84 f9 26 d1 26 b0 b1 c8 3 0 19 0 1 98 ff 1 98 8 ad ff 1 9f ff 2 96 d1 f8 ad ad f8
  //   a6 1 0 a0 0 1 ae 0 0 ff be ff 1 be ff ff 0 be 1 0 a0 40 80 c5 21 ff c3 a 0 1 ff bf ff a0 0 1 0 1 82
  //   83 c8 85 84 1 f3 3 c 21 90 20 e0 21 ff de 3 c b3 7 82 21 2c 82 83 42 54 83 85 1 3f 4 85 1 0 f8 0 fa
  //   fa 1d 1 6*0 7 ff a0 0 bf a3 ac 9f a3 ac 8f a3 ac 0 85 fd a5 f 90 3 8f 80 81 83 2 84 1 82 6 b0 5 b1
  //   25 1 a0 0 20 fc 3 0 ac ff 1 80 54 28 0 37 36 35 34 3e 1 1 1 8f 1 ff 3 2 3e 8f 8f af 7 80 21 c 81 4a
  //   34 ff fe b0 2 b1 2a 8 f9 65 fc f0 fc 7 22 fa 0 2 fb bb 50 fb b0 fa b1 a0 40 21 51 2 6f fe ff bb 92
  //   fe a0 40 21 51 2 fe ff 80 81 8f 84 3 c 21 fd 90 80 3 82 52 52 29 29 ff 7d 21 8c 34 fd 90 1 84 1 3f 4
  //   84 f9 26 cd 26 b0 b1 c4 4 0 8 ac ff 1 98 19 0 ff 1 9d ff 2 96 cd f8 ac ac ac f8 a4 1 a0 0 0 0 ff ba
  //   ff 1 ba ff ff 0 ba 1 0 a0 40 80 c1 21 ff bf a 0 1 ff bb ff a0 0 1 0 1 82 83 c4 85 84 1 ef 3 c 21 90
  //   20 dc 21 ff da 3 c af 7 82 21 2c 82 83 42 54 83 85 1 3f 4 85 1 0 f4 0 f6 f6 1d 1 10*0 3 3 2
endmodule

module ProgramCounter (
  input  [7:0] BUS_IN,
  input  CLOCK,
  input  RESET_DIS,
  input  LOAD_DIS,
  input  COUNT_EN,
  output [7:0] ADDRESS
);

  wire n74161_1_pin15;

  _74161 u_74161_1 (
    .pin1(RESET_DIS), .pin2(CLOCK), .pin3(BUS_IN[0]), .pin4(BUS_IN[1]), .pin5(BUS_IN[2]), .pin6(BUS_IN[3]),
    .pin7(COUNT_EN), .pin15(n74161_1_pin15), .pin14(ADDRESS[0]), .pin13(ADDRESS[1]), .pin12(ADDRESS[2]),
    .pin11(ADDRESS[3]), .pin10(COUNT_EN), .pin9(LOAD_DIS));
  _74161 u_74161_2 (
    .pin1(RESET_DIS), .pin2(CLOCK), .pin3(BUS_IN[4]), .pin4(BUS_IN[5]), .pin5(BUS_IN[6]), .pin6(BUS_IN[7]),
    .pin7(n74161_1_pin15), .pin14(ADDRESS[4]), .pin13(ADDRESS[5]), .pin12(ADDRESS[6]), .pin11(ADDRESS[7]),
    .pin10(n74161_1_pin15), .pin9(LOAD_DIS));  // open: pin15
endmodule

module FlagsMicrocodeROM (
  input  [7:0] OPCODE,
  input  [3:0] MICRO_COUNT,
  output [7:0] BUS_IN_FLAGS,
  output [7:0] BUS_OUT_FLAGS,
  output OUT_0,
  output OUT_1
);

  wire [7:2] rom_1_data;

  ROM #(.addrWidth(11)) rom_1 (.addr({OPCODE[6:0], MICRO_COUNT}), .data({rom_1_data, OUT_1, OUT_0}));
  Decoder #(.select(3)) decoder_1 (
    .out0(BUS_IN_FLAGS[0]), .out1(BUS_IN_FLAGS[1]), .out2(BUS_IN_FLAGS[2]), .out3(BUS_IN_FLAGS[3]),
    .out4(BUS_IN_FLAGS[4]), .out5(BUS_IN_FLAGS[5]), .out6(BUS_IN_FLAGS[6]), .out7(BUS_IN_FLAGS[7]),
    .sel(rom_1_data[7:5]));  // open: en
  Decoder #(.select(3)) decoder_2 (
    .out0(BUS_OUT_FLAGS[0]), .out1(BUS_OUT_FLAGS[1]), .out2(BUS_OUT_FLAGS[2]), .out3(BUS_OUT_FLAGS[3]),
    .out4(BUS_OUT_FLAGS[4]), .out5(BUS_OUT_FLAGS[5]), .out6(BUS_OUT_FLAGS[6]), .out7(BUS_OUT_FLAGS[7]),
    .sel(rom_1_data[4:2]));  // open: en

  // Notes on the sheet:
  //   contents of rom_1 (hex, n*v repeats v):
  //   16*0 2 15*ff 2 15*ff 2 15*ff 2 15*ff 29 29 1966*ff
endmodule

module RAMThing (
  input  [7:0] BUS_IN,
  input  [7:0] ADDRESS,
  input  CLOCK,
  input  LOAD_EN,
  input  OUTPUT_EN,
  output [7:0] BUS_OUT
);
endmodule

module MicrocodeCounter (
  input  CLOCK,
  input  SYNC_RESET_DIS,
  input  ASYNC_RESET_DIS,
  input  COUNT_EN,
  output [3:0] ADDRESS
);

  wire n74161_1_pin3;

  _74161 u_74161_1 (
    .pin1(ASYNC_RESET_DIS), .pin2(CLOCK), .pin3(n74161_1_pin3), .pin4(n74161_1_pin3), .pin5(n74161_1_pin3),
    .pin6(n74161_1_pin3), .pin7(COUNT_EN), .pin14(ADDRESS[0]), .pin13(ADDRESS[1]), .pin12(ADDRESS[2]),
    .pin11(ADDRESS[3]), .pin10(COUNT_EN), .pin9(SYNC_RESET_DIS));  // open: pin15
  // also tied to GND on the sheet: n74161_1_pin3
endmodule

module PlusOne (
  input  [7:0] VAL_IN,
  input  OUTPUT_EN,
  output [7:0] VAL_OUT
);

  wire [7:0] adder_1_out;

  Adder adder_1 (.a(VAL_IN), .b(8'h1), .out(adder_1_out));  // open: cin, cout
  assign VAL_OUT = OUTPUT_EN ? adder_1_out : 8'bz;  // Controlled_Buffer controlled_buffer_1
endmodule

module RLRegister (
  input  CLOCK,
  input  [7:0] DATA_IN,
  input  LOAD_DIS,
  input  RESET_EN,
  input  OUTPUT_DIS,
  output [7:0] DATA_OUT
);

  wire and_1_out, not_1_out, not_2_out;
  wire [7:0] n74273_1_pin2;

  and and_1 (and_1_out, ~LOAD_DIS, CLOCK);  // AND_Gate
  not not_1 (not_1_out, RESET_EN);
  not not_2 (not_2_out, OUTPUT_DIS);
  _74273 u_74273_1 (
    .pin1(not_1_out), .pin2(n74273_1_pin2[0]), .pin3(DATA_IN[0]), .pin4(DATA_IN[1]), .pin5(n74273_1_pin2[1]),
    .pin6(n74273_1_pin2[2]), .pin7(DATA_IN[2]), .pin8(DATA_IN[3]), .pin9(n74273_1_pin2[3]),
    .pin19(n74273_1_pin2[7]), .pin18(DATA_IN[7]), .pin17(DATA_IN[6]), .pin16(n74273_1_pin2[6]),
    .pin15(n74273_1_pin2[5]), .pin14(DATA_IN[5]), .pin13(DATA_IN[4]), .pin12(n74273_1_pin2[4]),
    .pin11(and_1_out));
  assign DATA_OUT = not_2_out ? n74273_1_pin2 : 8'bz;  // Controlled_Buffer controlled_buffer_1
endmodule

module RRegister (
  input  LOAD_CLOCK,
  input  [7:0] DATA_IN,
  input  RESET_DIS,
  output [7:0] DATA_OUT
);

  _74273 u_74273_1 (
    .pin1(RESET_DIS), .pin2(DATA_OUT[0]), .pin3(DATA_IN[0]), .pin4(DATA_IN[1]), .pin5(DATA_OUT[1]),
    .pin6(DATA_OUT[2]), .pin7(DATA_IN[2]), .pin8(DATA_IN[3]), .pin9(DATA_OUT[3]), .pin19(DATA_OUT[7]),
    .pin18(DATA_IN[7]), .pin17(DATA_IN[6]), .pin16(DATA_OUT[6]), .pin15(DATA_OUT[5]), .pin14(DATA_IN[5]),
    .pin13(DATA_IN[4]), .pin12(DATA_OUT[4]), .pin11(LOAD_CLOCK));
endmodule

module RegisterSelector (
  input  A,
  input  B,
  input  C,
  input  EN_OUT_1,
  input  DIS_OUT_2,
  input  DIS_OUT_3,
  output OUT_0,
  output OUT_1,
  output OUT_2,
  output OUT_3,
  output OUT_4,
  output OUT_5,
  output OUT_6,
  output OUT_7
);

  wire and_1_out;
  wire [7:0] decoder_1_out0;

  and and_1 (and_1_out, EN_OUT_1, ~DIS_OUT_2, ~DIS_OUT_3);  // AND_Gate
  Decoder #(.select(3)) decoder_1 (
    .out0(decoder_1_out0[0]), .out1(decoder_1_out0[1]), .out2(decoder_1_out0[2]), .out3(decoder_1_out0[3]),
    .out4(decoder_1_out0[4]), .out5(decoder_1_out0[5]), .out6(decoder_1_out0[6]), .out7(decoder_1_out0[7]),
    .sel({C, B, A}), .en(and_1_out));
  assign {OUT_7, OUT_6, OUT_5, OUT_4, OUT_3, OUT_2, OUT_1, OUT_0} = ~decoder_1_out0;  // NOT_Gate not_1, 8 bits wide
endmodule

module ALUROM (
  input  [7:0] OPCODE,
  input  [3:0] MICRO_COUNT,
  output [7:0] DATA
);

  ROM #(.addrWidth(11)) rom_1 (.addr({OPCODE[6:0], MICRO_COUNT}), .data(DATA));

  // Notes on the sheet:
  //   contents of rom_1 (hex, n*v repeats v):
  //   16*0 7a 15*ff 2 15*ff 2 15*ff 2 15*ff 29 29 1966*ff
endmodule

module MicrocodeROM (
  input  [7:0] OPCODE,
  input  [3:0] MICRO_COUNT,
  output [7:0] IO_FLAGS,
  output [7:0] ALU_FLAGS
);

  ROM #(.addrWidth(11)) rom_1 (.addr({OPCODE[6:0], MICRO_COUNT}), .data(IO_FLAGS));
  ROM #(.addrWidth(11)) rom_2 (.addr({OPCODE[6:0], MICRO_COUNT}), .data(ALU_FLAGS));

  // Notes on the sheet:
  //   contents of rom_1 (hex, n*v repeats v):
  //   16*0 77 175*ff 77 15*ff 77 559*ff 9 15*ff 19 15*ff 29 15*ff 39 143*ff 77 63*ff 44 a9 30*ff a9 991*ff
  //   contents of rom_2 (hex, n*v repeats v):
  //   7*80 0 8*80 60 175*ff e 15*ff 6 559*ff 76 15*ff 76 15*ff 76 15*ff 76 143*ff 76 63*ff 87 40 30*ff 40
  //   991*ff
endmodule

module SIPOShiftRegister (
  input  OUTPUT_DIS,
  input  RESET_DIS,
  input  SR_CLOCK,
  input  R_CLOCK,
  input  SERIAL_IN,
  output [7:0] PARALLEL_OUT,
  output SERIAL_OUT
);

  wire d_ff_1_q, d_ff_3_q, d_ff_5_q, d_ff_7_q, d_ff_9_q, d_ff_11_q, d_ff_13_q, not_1_out, not_2_out;
  wire [7:0] bit_extender_1_out, d_ff_2_q;

  not not_1 (not_1_out, OUTPUT_DIS);
  D_Flip_Flop d_ff_1 (.D(SERIAL_IN), .clk(SR_CLOCK), .Q(d_ff_1_q), .reset(not_2_out));  // open: Qn, preset
  not not_2 (not_2_out, RESET_DIS);
  D_Flip_Flop d_ff_2 (.D(d_ff_1_q), .clk(R_CLOCK), .Q(d_ff_2_q[0]));  // open: Qn, preset, reset
  D_Flip_Flop d_ff_3 (.D(d_ff_1_q), .clk(SR_CLOCK), .Q(d_ff_3_q), .reset(not_2_out));  // open: Qn, preset
  D_Flip_Flop d_ff_4 (.D(d_ff_3_q), .clk(R_CLOCK), .Q(d_ff_2_q[1]));  // open: Qn, preset, reset
  D_Flip_Flop d_ff_5 (.D(d_ff_3_q), .clk(SR_CLOCK), .Q(d_ff_5_q), .reset(not_2_out));  // open: Qn, preset
  D_Flip_Flop d_ff_6 (.D(d_ff_5_q), .clk(R_CLOCK), .Q(d_ff_2_q[2]));  // open: Qn, preset, reset
  D_Flip_Flop d_ff_7 (.D(d_ff_5_q), .clk(SR_CLOCK), .Q(d_ff_7_q), .reset(not_2_out));  // open: Qn, preset
  D_Flip_Flop d_ff_8 (.D(d_ff_7_q), .clk(R_CLOCK), .Q(d_ff_2_q[3]));  // open: Qn, preset, reset
  D_Flip_Flop d_ff_9 (.D(d_ff_7_q), .clk(SR_CLOCK), .Q(d_ff_9_q), .reset(not_2_out));  // open: Qn, preset
  D_Flip_Flop d_ff_10 (.D(d_ff_9_q), .clk(R_CLOCK), .Q(d_ff_2_q[4]));  // open: Qn, preset, reset
  D_Flip_Flop d_ff_11 (.D(d_ff_9_q), .clk(SR_CLOCK), .Q(d_ff_11_q), .reset(not_2_out));  // open: Qn, preset
  D_Flip_Flop d_ff_12 (.D(d_ff_11_q), .clk(R_CLOCK), .Q(d_ff_2_q[5]));  // open: Qn, preset, reset
  D_Flip_Flop d_ff_13 (.D(d_ff_11_q), .clk(SR_CLOCK), .Q(d_ff_13_q), .reset(not_2_out));  // open: Qn, preset
  D_Flip_Flop d_ff_14 (.D(d_ff_13_q), .clk(R_CLOCK), .Q(d_ff_2_q[6]));  // open: Qn, preset, reset
  D_Flip_Flop d_ff_15 (.D(d_ff_13_q), .clk(SR_CLOCK), .Q(SERIAL_OUT), .reset(not_2_out));  // open: Qn, preset
  D_Flip_Flop d_ff_16 (.D(SERIAL_OUT), .clk(R_CLOCK), .Q(d_ff_2_q[7]));  // open: Qn, preset, reset
  assign bit_extender_1_out = {{7{not_1_out}}, not_1_out};  // Bit_Extender bit_extender_1
  assign PARALLEL_OUT = bit_extender_1_out & d_ff_2_q;  // AND_Gate and_1, 8 bits wide
endmodule

module DisplayDecoder (
  input  [7:0] ROWS,
  input  [7:0] COLUMN,
  input  CLOCK,
  input  RESET_ASYNC,
  output [63:0] DISPLAY_OUT
);

  wire [7:0] and_1_out, and_2_out, and_3_out, and_4_out, and_5_out, and_6_out, and_7_out, and_8_out,
       bit_extender_1_out, bit_extender_2_out, bit_extender_3_out, bit_extender_4_out, bit_extender_5_out,
       bit_extender_6_out, bit_extender_7_out, bit_extender_8_out, or_1_out, or_2_out, or_3_out, or_4_out,
       or_5_out, or_6_out, or_7_out, or_8_out, or_9_out, or_10_out, or_11_out, or_12_out, or_13_out,
       or_14_out, or_15_out, or_16_out, register_1_q, register_2_q, register_3_q, register_4_q, register_5_q,
       register_6_q, register_7_q, register_8_q;

  assign bit_extender_1_out = {{7{COLUMN[0]}}, COLUMN[0]};  // Bit_Extender bit_extender_1
  assign bit_extender_2_out = {{7{COLUMN[1]}}, COLUMN[1]};  // Bit_Extender bit_extender_2
  assign bit_extender_3_out = {{7{COLUMN[2]}}, COLUMN[2]};  // Bit_Extender bit_extender_3
  assign bit_extender_4_out = {{7{COLUMN[3]}}, COLUMN[3]};  // Bit_Extender bit_extender_4
  assign bit_extender_5_out = {{7{COLUMN[4]}}, COLUMN[4]};  // Bit_Extender bit_extender_5
  assign bit_extender_6_out = {{7{COLUMN[5]}}, COLUMN[5]};  // Bit_Extender bit_extender_6
  assign bit_extender_7_out = {{7{COLUMN[6]}}, COLUMN[6]};  // Bit_Extender bit_extender_7
  assign bit_extender_8_out = {{7{COLUMN[7]}}, COLUMN[7]};  // Bit_Extender bit_extender_8
  assign and_1_out = bit_extender_1_out & ROWS;  // AND_Gate and_1, 8 bits wide
  assign and_2_out = bit_extender_2_out & ROWS;  // AND_Gate and_2, 8 bits wide
  assign and_3_out = bit_extender_3_out & ROWS;  // AND_Gate and_3, 8 bits wide
  assign and_4_out = bit_extender_4_out & ROWS;  // AND_Gate and_4, 8 bits wide
  assign and_5_out = bit_extender_5_out & ROWS;  // AND_Gate and_5, 8 bits wide
  assign and_6_out = bit_extender_6_out & ROWS;  // AND_Gate and_6, 8 bits wide
  assign and_7_out = bit_extender_7_out & ROWS;  // AND_Gate and_7, 8 bits wide
  assign and_8_out = bit_extender_8_out & ROWS;  // AND_Gate and_8, 8 bits wide
  assign or_1_out = register_1_q | and_1_out;  // OR_Gate or_1, 8 bits wide
  assign or_2_out = register_2_q | and_2_out;  // OR_Gate or_2, 8 bits wide
  assign or_3_out = register_3_q | and_3_out;  // OR_Gate or_3, 8 bits wide
  assign or_4_out = register_4_q | and_4_out;  // OR_Gate or_4, 8 bits wide
  assign or_5_out = register_5_q | and_5_out;  // OR_Gate or_5, 8 bits wide
  assign or_6_out = register_6_q | and_6_out;  // OR_Gate or_6, 8 bits wide
  assign or_7_out = register_7_q | and_7_out;  // OR_Gate or_7, 8 bits wide
  assign or_8_out = register_8_q | and_8_out;  // OR_Gate or_8, 8 bits wide
  Register register_1 (.D(or_1_out), .en(1'b1), .clk(CLOCK), .Q(register_1_q), .clr(RESET_ASYNC));
  Register register_2 (.D(or_2_out), .en(1'b1), .clk(CLOCK), .Q(register_2_q), .clr(RESET_ASYNC));
  Register register_3 (.D(or_3_out), .en(1'b1), .clk(CLOCK), .Q(register_3_q), .clr(RESET_ASYNC));
  Register register_4 (.D(or_4_out), .en(1'b1), .clk(CLOCK), .Q(register_4_q), .clr(RESET_ASYNC));
  Register register_5 (.D(or_5_out), .en(1'b1), .clk(CLOCK), .Q(register_5_q), .clr(RESET_ASYNC));
  Register register_6 (.D(or_6_out), .en(1'b1), .clk(CLOCK), .Q(register_6_q), .clr(RESET_ASYNC));
  Register register_7 (.D(or_7_out), .en(1'b1), .clk(CLOCK), .Q(register_7_q), .clr(RESET_ASYNC));
  Register register_8 (.D(or_8_out), .en(1'b1), .clk(CLOCK), .Q(register_8_q), .clr(RESET_ASYNC));
  assign or_9_out = register_1_q | or_1_out;  // OR_Gate or_9, 8 bits wide
  assign or_10_out = register_2_q | or_2_out;  // OR_Gate or_10, 8 bits wide
  assign or_11_out = register_3_q | or_3_out;  // OR_Gate or_11, 8 bits wide
  assign or_12_out = register_4_q | or_4_out;  // OR_Gate or_12, 8 bits wide
  assign or_13_out = register_5_q | or_5_out;  // OR_Gate or_13, 8 bits wide
  assign or_14_out = register_6_q | or_6_out;  // OR_Gate or_14, 8 bits wide
  assign or_15_out = register_7_q | or_7_out;  // OR_Gate or_15, 8 bits wide
  assign or_16_out = register_8_q | or_8_out;  // OR_Gate or_16, 8 bits wide
  assign DISPLAY_OUT = ~{or_16_out, or_15_out, or_14_out, or_13_out, or_12_out, or_11_out, or_10_out, or_9_out};  // NOT_Gate not_1, 64 bits wide
endmodule

module PISOShiftRegister (
  input  [7:0] PARALLEL_IN,
  input  LATCH,
  input  CLOCK,
  output SERIAL_OUT
);

  wire d_ff_1_q, d_ff_2_q, d_ff_3_q, d_ff_4_q, d_ff_5_q, d_ff_6_q, d_ff_7_q, decoder_1_out0, decoder_1_out1,
       decoder_2_out0, decoder_2_out1, decoder_3_out0, decoder_3_out1, decoder_4_out0, decoder_4_out1,
       decoder_5_out0, decoder_5_out1, decoder_6_out0, decoder_6_out1, decoder_7_out0, decoder_7_out1,
       decoder_8_out0, decoder_8_out1;

  D_Flip_Flop d_ff_1 (
    .D(1'b0), .clk(CLOCK), .Q(d_ff_1_q), .preset(decoder_1_out0), .reset(decoder_1_out1));  // open: Qn
  Decoder decoder_1 (.out0(decoder_1_out0), .out1(decoder_1_out1), .sel(PARALLEL_IN[7]), .en(LATCH));
  D_Flip_Flop d_ff_2 (
    .D(d_ff_1_q), .clk(CLOCK), .Q(d_ff_2_q), .preset(decoder_2_out0), .reset(decoder_2_out1));  // open: Qn
  Decoder decoder_2 (.out0(decoder_2_out0), .out1(decoder_2_out1), .sel(PARALLEL_IN[6]), .en(LATCH));
  D_Flip_Flop d_ff_3 (
    .D(d_ff_2_q), .clk(CLOCK), .Q(d_ff_3_q), .preset(decoder_3_out0), .reset(decoder_3_out1));  // open: Qn
  Decoder decoder_3 (.out0(decoder_3_out0), .out1(decoder_3_out1), .sel(PARALLEL_IN[5]), .en(LATCH));
  D_Flip_Flop d_ff_4 (
    .D(d_ff_3_q), .clk(CLOCK), .Q(d_ff_4_q), .preset(decoder_4_out0), .reset(decoder_4_out1));  // open: Qn
  Decoder decoder_4 (.out0(decoder_4_out0), .out1(decoder_4_out1), .sel(PARALLEL_IN[4]), .en(LATCH));
  D_Flip_Flop d_ff_5 (
    .D(d_ff_4_q), .clk(CLOCK), .Q(d_ff_5_q), .preset(decoder_5_out0), .reset(decoder_5_out1));  // open: Qn
  Decoder decoder_5 (.out0(decoder_5_out0), .out1(decoder_5_out1), .sel(PARALLEL_IN[3]), .en(LATCH));
  D_Flip_Flop d_ff_6 (
    .D(d_ff_5_q), .clk(CLOCK), .Q(d_ff_6_q), .preset(decoder_6_out0), .reset(decoder_6_out1));  // open: Qn
  Decoder decoder_6 (.out0(decoder_6_out0), .out1(decoder_6_out1), .sel(PARALLEL_IN[2]), .en(LATCH));
  D_Flip_Flop d_ff_7 (
    .D(d_ff_6_q), .clk(CLOCK), .Q(d_ff_7_q), .preset(decoder_7_out0), .reset(decoder_7_out1));  // open: Qn
  Decoder decoder_7 (.out0(decoder_7_out0), .out1(decoder_7_out1), .sel(PARALLEL_IN[1]), .en(LATCH));
  D_Flip_Flop d_ff_8 (
    .D(d_ff_7_q), .clk(CLOCK), .Q(SERIAL_OUT), .preset(decoder_8_out0), .reset(decoder_8_out1));  // open: Qn
  Decoder decoder_8 (.out0(decoder_8_out0), .out1(decoder_8_out1), .sel(PARALLEL_IN[0]), .en(LATCH));
endmodule
