# Fritzing sketch ProgramCounter (saved by Fritzing 0.9.10b)
breadboards: 1

parts:
  IC1 = DIP - 20 pins [chip_label=74LS245 package="DIP (Dual Inline) [THT]"]
  74LS1 = 74LS161 [chip_label=74LS161 package="DIP (Dual Inline) [THT]"]
  LED1 = LED - 5mm [color="Green (555nm)" current=0.030 package="5 mm [THT]"]
  LED2 = LED - 5mm [color="Green (555nm)" current=0.030 package="5 mm [THT]"]
  LED3 = LED - 5mm [color="Green (555nm)" current=0.030 package="5 mm [THT]"]
  LED4 = LED - 5mm [color="Green (555nm)" current=0.030 package="5 mm [THT]"]
  R4 = Resistor [tolerance=±5% power=0.25 resistance=1k package=THT]
  R1 = Resistor [tolerance=±5% power=0.25 resistance=1k package=THT]
  R2 = Resistor [tolerance=±5% power=0.25 resistance=1k package=THT]
  R3 = Resistor [tolerance=±5% power=0.25 resistance=1k package=THT]

nets:
  GND: IC1.DIR, IC1.GND, IC1.OE, 74LS1.ENP, 74LS1.GND, 74LS1.ENT, LED1.cathode, LED2.cathode, LED3.cathode, LED4.cathode
  N1: IC1.A1, 74LS1.In_1
  N2: IC1.A2, 74LS1.In_2
  N3: IC1.A3, 74LS1.In_3
  N4: IC1.A4, 74LS1.In_4
  N5: IC1.B4, 74LS1.Out_4, R3.Pin_1
  N6: IC1.B3, 74LS1.Out_3, R2.Pin_1
  N7: IC1.B2, 74LS1.Out_2, R1.Pin_1
  N8: IC1.B1, 74LS1.Out_1, R4.Pin_1
  VCC: IC1.VCC, 74LS1.-CLR, 74LS1.-LOAD, 74LS1.VCC
  N9: LED1.anode, R4.Pin_0
  N10: LED2.anode, R1.Pin_0
  N11: LED4.anode, R3.Pin_0

custom parts:
  DIP - 20 pins: A DIP stand-in part for whatever IC you want. With 20 pins on a 300mil dual inline package (DIP) footprint.
  74LS161: 74LS161 synchronous counter with asynchronous clear
