# Fritzing sketch ProgramROM (saved by Fritzing 0.9.10b)
breadboards: 2

parts:
  U1 = ZIFSOCKET-40-6 [package=dil40-6-zif_socket]
  U2 = ZIFSOCKET-40-6 [package=dil40-6-zif_socket]

nets:
  N1: U1.P$1, U1.P$2, U1.P$10, U1.P$14, U2.P$1, U2.P$2, U2.P$14
  N2: U1.P$3, U2.P$3
  N3: U1.P$9, U2.P$9
  N4: U1.P$32, U2.P$32
  N5: U1.P$33, U1.P$35, U1.P$36, U1.P$37, U1.P$38, U2.P$33, U2.P$35, U2.P$36, U2.P$37, U2.P$38
  N6: U1.P$34, U2.P$34
  N7: U1.P$39, U1.P$40, U2.P$39, U2.P$40
