# Fritzing sketch ProgramROMWithTristateV2 (saved by Fritzing 0.9.10b)
breadboards: 2

parts:
  IC1 = DIP - 20 pins [chip_label=74LS245 package="DIP (Dual Inline) [THT]"]
  U1 = ZIFSOCKET-40-6 [package=dil40-6-zif_socket]
  U2 = ZIFSOCKET-40-6 [package=dil40-6-zif_socket]

nets:
  N1: IC1.DIR, IC1.GND, U1.P$32, U1.P$33, U1.P$34, U1.P$35, U1.P$36, U1.P$37, U1.P$38, U2.P$1, U2.P$2, U2.P$14, U2.P$32, U2.P$33, U2.P$34, U2.P$35, U2.P$36, U2.P$37, U2.P$38
  N2: U1.P$1, U1.P$2, U1.P$14
  N3: U1.P$39, U1.P$40, U2.P$10, U2.P$39, U2.P$40

custom parts:
  DIP - 20 pins: A DIP stand-in part for whatever IC you want. With 20 pins on a 300mil dual inline package (DIP) footprint.
