# Fritzing sketch RegistersAB (saved by Fritzing 0.9.10b)
breadboards: 2

parts:
  IC1 = DIP - 20 pins [chip_label=74LS245 package="DIP (Dual Inline) [THT]"]
  IC2 = DIP - 16 pins [chip_label=74LS173 package="DIP (Dual Inline) [THT]"]
  IC3 = DIP - 16 pins [chip_label=74LS173 package="DIP (Dual Inline) [THT]"]
  IC4 = DIP - 20 pins [chip_label=74LS245 package="DIP (Dual Inline) [THT]"]
  IC5 = DIP - 16 pins [chip_label=74LS173 package="DIP (Dual Inline) [THT]"]
  IC6 = DIP - 16 pins [chip_label=74LS173 package="DIP (Dual Inline) [THT]"]

nets:
  N1: IC1.A1, IC3.1Q, IC4.A1, IC6.1Q
  N2: IC1.A2, IC3.2Q, IC4.A2, IC6.2Q
  N3: IC1.A3, IC3.3Q, IC4.A3, IC6.3Q
  N4: IC1.A4, IC3.4Q, IC4.A4, IC6.4Q
  N5: IC1.A5, IC2.1Q, IC4.A5, IC5.1Q
  N6: IC1.A6, IC2.2Q, IC4.A6, IC5.2Q
  N7: IC1.A7, IC2.3Q, IC4.A7, IC5.3Q
  N8: IC1.A8, IC2.4Q, IC4.A8, IC5.4Q
  N9: IC1.B8, IC2.4D, IC4.B8, IC5.4D
  N10: IC1.B7, IC2.3D, IC4.B7, IC5.3D
  N11: IC1.B6, IC2.2D, IC4.B6, IC5.2D
  N12: IC1.B5, IC2.1D, IC4.B5, IC5.1D
  N13: IC1.B4, IC3.4D, IC4.B4, IC6.4D
  N14: IC1.B3, IC3.3D, IC4.B3, IC6.3D
  N15: IC1.B2, IC3.2D, IC4.B2, IC6.2D
  N16: IC1.B1, IC3.1D, IC4.B1, IC6.1D

custom parts:
  DIP - 20 pins: A DIP stand-in part for whatever IC you want. With 20 pins on a 300mil dual inline package (DIP) footprint.
  DIP - 16 pins: A DIP stand-in part for whatever IC you want. With 16 pins on a 300mil dual inline package (DIP) footprint.
